// Logisim project Base Computer Componants.circ as structural Verilog: 5 circuits, main circuit arithmitic
module arithmitic (
);

  wire and_1_out, and_2_out, and_3_out, and_4_out, and_5_out, and_6_out, and_7_out, and_8_out, and_9_out,
       and_10_out, and_11_out, and_12_out, and_13_out, and_14_out, and_15_out, and_16_out, and_17_out,
       and_18_out, and_19_out, and_20_out, and_21_out, and_22_out, or_1_out, or_2_out, or_3_out, or_4_out,
       or_5_out, or_6_out, or_7_out, pull_resistor_1_node, pull_resistor_2_node, transistor_1_out,
       transistor_2_out, transistor_3_out, transistor_4_out, transistor_5_out, transistor_6_out,
       transistor_7_out, transistor_8_out, undriven, undriven_2, undriven_3, undriven_4, undriven_5,
       undriven_6, undriven_7, undriven_8, undriven_9, undriven_10, undriven_11, undriven_12, undriven_13,
       undriven_14, undriven_15, undriven_16, xor_1_out, xor_2_out, xor_3_out, xor_4_out, xor_5_out,
       xor_6_out, xor_7_out, xor_8_out, xor_9_out, xor_10_out, xor_11_out, xor_12_out, xor_13_out,
       xor_14_out, xor_15_out;

  Transistor #(.\type ("n")) transistor_1 (.in(undriven_6), .out(transistor_1_out), .gate(pull_resistor_1_node));
  Transistor #(.\type ("n")) transistor_2 (.in(undriven_5), .out(transistor_2_out), .gate(pull_resistor_1_node));
  Transistor #(.\type ("n")) transistor_3 (.in(undriven_8), .out(transistor_3_out), .gate(pull_resistor_1_node));
  Transistor #(.\type ("n")) transistor_4 (.in(undriven), .out(transistor_4_out), .gate(pull_resistor_1_node));
  Transistor #(.\type ("n")) transistor_5 (.in(undriven_2), .out(transistor_5_out), .gate(pull_resistor_1_node));
  Transistor #(.\type ("n")) transistor_6 (.in(undriven_7), .out(transistor_6_out), .gate(pull_resistor_1_node));
  Transistor #(.\type ("n")) transistor_7 (.in(undriven_3), .out(transistor_7_out), .gate(pull_resistor_1_node));
  Transistor #(.\type ("n")) transistor_8 (.in(undriven_4), .out(transistor_8_out), .gate(pull_resistor_1_node));
  xor xor_1 (xor_1_out, 1'b1, ~undriven_5);  // XOR_Gate
  and and_1 (and_1_out, 1'b1, ~undriven_5);  // AND_Gate
  and and_2 (and_2_out, and_1_out, ~undriven_6);  // AND_Gate
  xor xor_2 (xor_2_out, and_1_out, ~undriven_6);  // XOR_Gate
  and and_3 (and_3_out, and_2_out, ~undriven_4);  // AND_Gate
  xor xor_3 (xor_3_out, and_2_out, ~undriven_4);  // XOR_Gate
  xor xor_4 (xor_4_out, and_3_out, ~undriven_3);  // XOR_Gate
  and and_4 (and_4_out, and_3_out, ~undriven_3);  // AND_Gate
  and and_5 (and_5_out, and_4_out, ~undriven_7);  // AND_Gate
  xor xor_5 (xor_5_out, and_4_out, ~undriven_7);  // XOR_Gate
  xor xor_6 (xor_6_out, and_5_out, ~undriven_2);  // XOR_Gate
  and and_6 (and_6_out, and_5_out, ~undriven_2);  // AND_Gate
  and and_7 (and_7_out, and_6_out, ~undriven);  // AND_Gate
  xor xor_7 (xor_7_out, and_6_out, ~undriven);  // XOR_Gate
  xor xor_8 (xor_8_out, and_7_out, ~undriven_8);  // XOR_Gate
  Transistor #(.\type ("n")) transistor_9 (.in(xor_1_out), .out(transistor_2_out), .gate(pull_resistor_2_node));
  Transistor #(.\type ("n")) transistor_10 (.in(xor_2_out), .out(transistor_1_out), .gate(pull_resistor_2_node));
  Transistor #(.\type ("n")) transistor_11 (.in(xor_3_out), .out(transistor_8_out), .gate(pull_resistor_2_node));
  Transistor #(.\type ("n")) transistor_12 (.in(xor_4_out), .out(transistor_7_out), .gate(pull_resistor_2_node));
  Transistor #(.\type ("n")) transistor_13 (.in(xor_5_out), .out(transistor_6_out), .gate(pull_resistor_2_node));
  Transistor #(.\type ("n")) transistor_14 (.in(xor_6_out), .out(transistor_5_out), .gate(pull_resistor_2_node));
  Transistor #(.\type ("n")) transistor_15 (.in(xor_7_out), .out(transistor_4_out), .gate(pull_resistor_2_node));
  Transistor #(.\type ("n")) transistor_16 (.in(xor_8_out), .out(transistor_3_out), .gate(pull_resistor_2_node));
  Pull_Resistor pull_resistor_1 (.node(pull_resistor_1_node));
  Pull_Resistor pull_resistor_2 (.node(pull_resistor_2_node));
  and and_8 (and_8_out, transistor_2_out, undriven_16);
  and and_9 (and_9_out, and_8_out, undriven_15);
  xor xor_9 (xor_9_out, and_8_out, undriven_15);
  and and_10 (and_10_out, xor_9_out, transistor_1_out);
  or or_1 (or_1_out, and_9_out, and_10_out);
  xor xor_10 (xor_10_out, or_1_out, undriven_14);
  and and_11 (and_11_out, or_1_out, undriven_14);
  and and_12 (and_12_out, xor_10_out, transistor_8_out);
  or or_2 (or_2_out, and_11_out, and_12_out);
  xor xor_11 (xor_11_out, or_2_out, undriven_13);
  and and_13 (and_13_out, or_2_out, undriven_13);
  and and_14 (and_14_out, xor_11_out, transistor_7_out);
  or or_3 (or_3_out, and_13_out, and_14_out);
  and and_15 (and_15_out, or_3_out, undriven_12);
  xor xor_12 (xor_12_out, or_3_out, undriven_12);
  and and_16 (and_16_out, xor_12_out, transistor_6_out);
  or or_4 (or_4_out, and_15_out, and_16_out);
  and and_17 (and_17_out, or_4_out, undriven_11);
  xor xor_13 (xor_13_out, or_4_out, undriven_11);
  and and_18 (and_18_out, xor_13_out, transistor_5_out);
  or or_5 (or_5_out, and_17_out, and_18_out);
  xor xor_14 (xor_14_out, or_5_out, undriven_10);
  and and_19 (and_19_out, or_5_out, undriven_10);
  and and_20 (and_20_out, xor_14_out, transistor_4_out);
  or or_6 (or_6_out, and_19_out, and_20_out);
  xor xor_15 (xor_15_out, or_6_out, undriven_9);
  and and_21 (and_21_out, or_6_out, undriven_9);
  and and_22 (and_22_out, xor_15_out, transistor_3_out);
  or or_7 (or_7_out, and_21_out, and_22_out);
  // XOR_Gate xor_16 has open pins: in0=transistor_2_out, in1=undriven_16, out=open
  // XOR_Gate xor_17 has open pins: in0=xor_9_out, in1=transistor_1_out, out=open
  // XOR_Gate xor_18 has open pins: in0=xor_10_out, in1=transistor_8_out, out=open
  // XOR_Gate xor_19 has open pins: in0=xor_11_out, in1=transistor_7_out, out=open
  // XOR_Gate xor_20 has open pins: in0=xor_12_out, in1=transistor_6_out, out=open
  // XOR_Gate xor_21 has open pins: in0=xor_13_out, in1=transistor_5_out, out=open
  // XOR_Gate xor_22 has open pins: in0=xor_14_out, in1=transistor_4_out, out=open
  // XOR_Gate xor_23 has open pins: in0=xor_15_out, in1=transistor_3_out, out=open
endmodule

module comparer (
);

  wire and_1_out, and_2_out, and_3_out, and_4_out, and_5_out, and_6_out, and_7_out, and_8_out, and_9_out,
       and_10_out, and_11_out, and_12_out, and_13_out, and_14_out, and_15_out, and_16_out, and_17_out,
       and_18_out, and_19_out, and_20_out, and_21_out, and_22_out, and_23_out, or_1_out, or_2_out, or_3_out,
       or_4_out, or_5_out, or_6_out, or_7_out, or_8_out, or_9_out, or_10_out, pull_resistor_2_node,
       pull_resistor_10_node, pull_resistor_12_node, pull_resistor_14_node, transistor_1_out,
       transistor_2_out, transistor_3_out, transistor_4_out, transistor_5_out, transistor_6_out,
       transistor_7_out, transistor_8_out, transistor_9_out, transistor_10_out, transistor_11_out,
       transistor_12_out, transistor_13_out, transistor_14_out, transistor_15_out, transistor_16_out,
       transistor_17_out, transistor_19_out, transistor_20_out, transistor_21_out, transistor_22_out,
       transistor_23_out, transistor_24_out, transistor_25_out, transistor_27_out, transistor_29_out,
       undriven, undriven_2, undriven_3, undriven_4, undriven_5, undriven_6, undriven_7, undriven_8,
       undriven_9, undriven_10, undriven_11, undriven_12, undriven_13, undriven_14, undriven_15, undriven_16;

  Transistor #(.\type ("n"), .gate("br")) transistor_1 (.in(undriven), .out(transistor_1_out), .gate(and_1_out));
  Transistor #(.\type ("n")) transistor_2 (.in(undriven_16), .out(transistor_2_out), .gate(and_1_out));
  Transistor #(.\type ("n"), .gate("br")) transistor_3 (.in(undriven_2), .out(transistor_3_out), .gate(and_2_out));
  Transistor #(.\type ("n")) transistor_4 (.in(undriven_9), .out(transistor_4_out), .gate(and_2_out));
  Transistor #(.\type ("n"), .gate("br")) transistor_5 (.in(undriven_3), .out(transistor_5_out), .gate(and_3_out));
  Transistor #(.\type ("n")) transistor_6 (.in(undriven_10), .out(transistor_6_out), .gate(and_3_out));
  Transistor #(.\type ("n"), .gate("br")) transistor_7 (.in(undriven_4), .out(transistor_7_out), .gate(and_4_out));
  Transistor #(.\type ("n")) transistor_8 (.in(undriven_11), .out(transistor_8_out), .gate(and_4_out));
  Transistor #(.\type ("n"), .gate("br")) transistor_9 (.in(undriven_5), .out(transistor_9_out), .gate(and_5_out));
  Transistor #(.\type ("n")) transistor_10 (.in(undriven_12), .out(transistor_10_out), .gate(and_5_out));
  Transistor #(.\type ("n"), .gate("br")) transistor_11 (.in(undriven_6), .out(transistor_11_out), .gate(and_6_out));
  Transistor #(.\type ("n")) transistor_12 (.in(undriven_13), .out(transistor_12_out), .gate(and_6_out));
  Transistor #(.\type ("n"), .gate("br")) transistor_13 (.in(undriven_7), .out(transistor_13_out), .gate(and_7_out));
  Transistor #(.\type ("n")) transistor_14 (.in(undriven_14), .out(transistor_14_out), .gate(and_7_out));
  Transistor #(.gate("br")) transistor_15 (.in(undriven_8), .out(transistor_15_out), .gate(or_8_out));
  Transistor transistor_16 (.in(undriven_15), .out(transistor_16_out), .gate(or_8_out));
  Pull_Resistor pull_resistor_1 (.node(transistor_1_out));
  and and_1 (and_1_out, or_2_out, ~or_1_out);  // AND_Gate
  and and_2 (and_2_out, or_3_out, ~or_2_out);  // AND_Gate
  and and_3 (and_3_out, or_4_out, ~or_3_out);  // AND_Gate
  and and_4 (and_4_out, or_5_out, ~or_4_out);  // AND_Gate
  and and_5 (and_5_out, or_6_out, ~or_5_out);  // AND_Gate
  and and_6 (and_6_out, or_7_out, ~or_6_out);  // AND_Gate
  and and_7 (and_7_out, or_8_out, ~or_7_out);  // AND_Gate
  Transistor #(.\type ("n"), .gate("br")) transistor_17 (.in(undriven), .out(transistor_17_out), .gate(or_2_out));
  Pull_Resistor pull_resistor_2 (.node(pull_resistor_2_node));
  Transistor #(.\type ("n")) transistor_18 (.in(undriven_16), .out(pull_resistor_2_node), .gate(or_2_out));
  Pull_Resistor #(.pull(1)) pull_resistor_3 (.node(transistor_17_out));
  Transistor #(.\type ("n"), .gate("br")) transistor_19 (.in(undriven_2), .out(transistor_19_out), .gate(or_3_out));
  Transistor #(.\type ("n")) transistor_20 (.in(undriven_9), .out(transistor_20_out), .gate(or_3_out));
  Pull_Resistor pull_resistor_4 (.node(transistor_20_out));
  Pull_Resistor #(.pull(1)) pull_resistor_5 (.node(transistor_19_out));
  Transistor #(.\type ("n"), .gate("br")) transistor_21 (.in(undriven_3), .out(transistor_21_out), .gate(or_4_out));
  Transistor #(.\type ("n")) transistor_22 (.in(undriven_10), .out(transistor_22_out), .gate(or_4_out));
  Pull_Resistor pull_resistor_6 (.node(transistor_22_out));
  Pull_Resistor #(.pull(1)) pull_resistor_7 (.node(transistor_21_out));
  Transistor #(.\type ("n"), .gate("br")) transistor_23 (.in(undriven_4), .out(transistor_23_out), .gate(or_5_out));
  Transistor #(.\type ("n")) transistor_24 (.in(undriven_11), .out(transistor_24_out), .gate(or_5_out));
  Pull_Resistor pull_resistor_8 (.node(transistor_24_out));
  Pull_Resistor #(.pull(1)) pull_resistor_9 (.node(transistor_23_out));
  Transistor #(.\type ("n"), .gate("br")) transistor_25 (.in(undriven_5), .out(transistor_25_out), .gate(or_6_out));
  Pull_Resistor pull_resistor_10 (.node(pull_resistor_10_node));
  Transistor #(.\type ("n")) transistor_26 (.in(undriven_12), .out(pull_resistor_10_node), .gate(or_6_out));
  Pull_Resistor #(.pull(1)) pull_resistor_11 (.node(transistor_25_out));
  Transistor #(.\type ("n"), .gate("br")) transistor_27 (.in(undriven_6), .out(transistor_27_out), .gate(or_7_out));
  Pull_Resistor pull_resistor_12 (.node(pull_resistor_12_node));
  Transistor #(.\type ("n")) transistor_28 (.in(undriven_13), .out(pull_resistor_12_node), .gate(or_7_out));
  Pull_Resistor #(.pull(1)) pull_resistor_13 (.node(transistor_27_out));
  Transistor #(.\type ("n"), .gate("br")) transistor_29 (.in(undriven_7), .out(transistor_29_out), .gate(or_8_out));
  Pull_Resistor pull_resistor_14 (.node(pull_resistor_14_node));
  Transistor #(.\type ("n")) transistor_30 (.in(undriven_14), .out(pull_resistor_14_node), .gate(or_8_out));
  Pull_Resistor #(.pull(1)) pull_resistor_15 (.node(transistor_29_out));
  Pull_Resistor pull_resistor_16 (.node(transistor_3_out));
  Pull_Resistor pull_resistor_17 (.node(transistor_5_out));
  Pull_Resistor pull_resistor_18 (.node(transistor_7_out));
  Pull_Resistor pull_resistor_19 (.node(transistor_9_out));
  Pull_Resistor pull_resistor_20 (.node(transistor_11_out));
  Pull_Resistor pull_resistor_21 (.node(transistor_13_out));
  and and_8 (and_8_out, ~transistor_17_out, ~pull_resistor_2_node);  // AND_Gate
  and and_9 (and_9_out, pull_resistor_2_node, transistor_17_out);
  and and_10 (and_10_out, ~transistor_19_out, ~transistor_20_out);  // AND_Gate
  and and_11 (and_11_out, transistor_20_out, transistor_19_out);
  and and_12 (and_12_out, ~transistor_21_out, ~transistor_22_out);  // AND_Gate
  and and_13 (and_13_out, transistor_22_out, transistor_21_out);
  and and_14 (and_14_out, ~transistor_23_out, ~transistor_24_out);  // AND_Gate
  and and_15 (and_15_out, transistor_24_out, transistor_23_out);
  and and_16 (and_16_out, ~transistor_25_out, ~pull_resistor_10_node);  // AND_Gate
  and and_17 (and_17_out, pull_resistor_10_node, transistor_25_out);
  and and_18 (and_18_out, ~transistor_27_out, ~pull_resistor_12_node);  // AND_Gate
  and and_19 (and_19_out, pull_resistor_12_node, transistor_27_out);
  and and_20 (and_20_out, ~transistor_29_out, ~pull_resistor_14_node);  // AND_Gate
  and and_21 (and_21_out, pull_resistor_14_node, transistor_29_out);
  and and_22 (and_22_out, ~undriven_8, ~undriven_15);  // AND_Gate
  and and_23 (and_23_out, undriven_15, undriven_8);
  Pull_Resistor pull_resistor_22 (.node(transistor_15_out));
  or or_1 (or_1_out, and_8_out, and_9_out);
  Pull_Resistor pull_resistor_23 (.node(transistor_2_out));
  Pull_Resistor pull_resistor_24 (.node(transistor_4_out));
  Pull_Resistor pull_resistor_25 (.node(transistor_6_out));
  Pull_Resistor pull_resistor_26 (.node(transistor_8_out));
  Pull_Resistor pull_resistor_27 (.node(transistor_10_out));
  Pull_Resistor pull_resistor_28 (.node(transistor_12_out));
  Pull_Resistor pull_resistor_29 (.node(transistor_14_out));
  or or_2 (or_2_out, and_10_out, and_11_out);
  or or_3 (or_3_out, and_12_out, and_13_out);
  or or_4 (or_4_out, and_14_out, and_15_out);
  or or_5 (or_5_out, and_16_out, and_17_out);
  or or_6 (or_6_out, and_18_out, and_19_out);
  or or_7 (or_7_out, and_20_out, and_21_out);
  or or_8 (or_8_out, and_22_out, and_23_out);
  or or_9 (or_9_out, transistor_1_out, transistor_3_out, transistor_5_out, transistor_7_out, transistor_9_out, transistor_11_out, transistor_13_out, transistor_15_out);
  or or_10 (or_10_out, transistor_2_out, transistor_4_out, transistor_6_out, transistor_8_out, transistor_10_out, transistor_12_out, transistor_14_out, transistor_16_out);
  Pull_Resistor pull_resistor_30 (.node(transistor_16_out));
endmodule

module divider (
);

  wire and_1_out, and_2_out, and_3_out, and_4_out, and_5_out, and_6_out, and_7_out, and_8_out, and_9_out,
       and_10_out, and_11_out, and_12_out, and_13_out, and_14_out, and_15_out, and_16_out, and_17_out,
       and_18_out, and_19_out, and_20_out, and_21_out, and_22_out, and_23_out, and_24_out, and_25_out,
       and_26_out, and_27_out, and_28_out, and_29_out, and_30_out, and_31_out, and_32_out, and_33_out,
       and_34_out, and_35_out, and_36_out, and_37_out, and_38_out, and_39_out, and_40_out, and_41_out,
       and_42_out, and_43_out, and_44_out, and_45_out, and_46_out, and_47_out, and_48_out, and_49_out,
       and_50_out, and_51_out, and_52_out, and_53_out, and_54_out, and_55_out, and_56_out, and_57_out,
       and_58_out, and_59_out, and_60_out, and_61_out, and_62_out, and_63_out, and_64_out, comparator_1_gt,
       comparator_2_gt, comparator_3_gt, comparator_4_gt, comparator_5_gt, comparator_6_gt, comparator_7_gt,
       comparator_8_gt, not_1_out, not_2_out, not_3_out, not_4_out, not_5_out, not_6_out, not_7_out,
       not_8_out, pull_resistor_1_node, pull_resistor_2_node, pull_resistor_3_node, pull_resistor_4_node,
       pull_resistor_5_node, pull_resistor_6_node, pull_resistor_7_node, pull_resistor_9_node,
       pull_resistor_10_node, pull_resistor_11_node, pull_resistor_12_node, pull_resistor_13_node,
       pull_resistor_14_node, pull_resistor_17_node, pull_resistor_18_node, pull_resistor_19_node,
       pull_resistor_20_node, pull_resistor_21_node, pull_resistor_25_node, pull_resistor_26_node,
       pull_resistor_27_node, pull_resistor_28_node, pull_resistor_33_node, pull_resistor_34_node,
       pull_resistor_35_node, pull_resistor_41_node, pull_resistor_42_node, pull_resistor_49_node,
       subtractor_1_bout, subtractor_2_bout, subtractor_3_bout, subtractor_4_bout, subtractor_5_bout,
       subtractor_6_bout, subtractor_7_bout, subtractor_9_bout, subtractor_10_bout, subtractor_11_bout,
       subtractor_12_bout, subtractor_13_bout, subtractor_14_bout, subtractor_15_bout, subtractor_17_bout,
       subtractor_18_bout, subtractor_19_bout, subtractor_20_bout, subtractor_21_bout, subtractor_22_bout,
       subtractor_23_bout, subtractor_25_bout, subtractor_26_bout, subtractor_27_bout, subtractor_28_bout,
       subtractor_29_bout, subtractor_30_bout, subtractor_31_bout, subtractor_33_bout, subtractor_34_bout,
       subtractor_35_bout, subtractor_36_bout, subtractor_37_bout, subtractor_38_bout, subtractor_39_bout,
       subtractor_41_bout, subtractor_42_bout, subtractor_43_bout, subtractor_44_bout, subtractor_45_bout,
       subtractor_46_bout, subtractor_47_bout, subtractor_49_bout, subtractor_50_bout, subtractor_51_bout,
       subtractor_52_bout, subtractor_53_bout, subtractor_54_bout, subtractor_55_bout, subtractor_57_bout,
       subtractor_57_out, subtractor_58_bout, subtractor_58_out, subtractor_59_bout, subtractor_59_out,
       subtractor_60_bout, subtractor_60_out, subtractor_61_bout, subtractor_61_out, subtractor_62_bout,
       subtractor_62_out, subtractor_63_bout, subtractor_63_out, subtractor_64_out;
  wire [6:0] pull_resistor_8_node;
  wire [7:0] subtractor_1_out, subtractor_9_out, subtractor_17_out, subtractor_25_out, subtractor_33_out,
       subtractor_41_out, subtractor_49_out;
  wire [8:0] bit_extender_13_out, bit_extender_14_out, shifter_7_out;
  wire [9:0] bit_extender_11_out, bit_extender_12_out, shifter_6_out;
  wire [10:0] bit_extender_9_out, bit_extender_10_out, shifter_5_out;
  wire [11:0] bit_extender_7_out, bit_extender_8_out, shifter_4_out;
  wire [12:0] bit_extender_5_out, bit_extender_6_out, shifter_3_out;
  wire [13:0] bit_extender_3_out, bit_extender_4_out, shifter_2_out;
  wire [14:0] bit_extender_1_out, bit_extender_2_out, shifter_1_out;

  assign bit_extender_1_out = {{7{1'b0}}, 8'hc};  // Bit_Extender bit_extender_1
  Shifter #(.width(15)) shifter_1 (.in(bit_extender_2_out), .\dist (4'b0111), .out(shifter_1_out));
  Pull_Resistor pull_resistor_1 (.node(pull_resistor_1_node));
  and and_1 (and_1_out, pull_resistor_1_node, not_1_out);
  Pull_Resistor pull_resistor_2 (.node(pull_resistor_2_node));
  and and_2 (and_2_out, pull_resistor_2_node, not_1_out);
  Pull_Resistor pull_resistor_3 (.node(pull_resistor_3_node));
  and and_3 (and_3_out, pull_resistor_3_node, not_1_out);
  Pull_Resistor pull_resistor_4 (.node(pull_resistor_4_node));
  and and_4 (and_4_out, pull_resistor_4_node, not_1_out);
  Pull_Resistor pull_resistor_5 (.node(pull_resistor_5_node));
  and and_5 (and_5_out, pull_resistor_5_node, not_1_out);
  Pull_Resistor pull_resistor_6 (.node(pull_resistor_6_node));
  and and_6 (and_6_out, pull_resistor_6_node, not_1_out);
  Pull_Resistor pull_resistor_7 (.node(pull_resistor_7_node));
  and and_7 (and_7_out, pull_resistor_7_node, not_1_out);
  Pull_Resistor pull_resistor_8 (.node(pull_resistor_8_node[0]));
  and and_8 (and_8_out, pull_resistor_8_node[0], not_1_out);
  assign bit_extender_2_out = {{7{1'b0}}, {1'b0, pull_resistor_8_node}};  // Bit_Extender bit_extender_2
  not not_1 (not_1_out, comparator_1_gt);
  Comparator #(.width(15), .mode("unsigned")) comparator_1 (
    .a(shifter_1_out), .b(bit_extender_1_out), .gt(comparator_1_gt));  // open: eq, lt
  Subtractor #(.width(1)) subtractor_1 (
    .a(1'b0), .b(and_1_out), .out(subtractor_1_out[0]), .bout(subtractor_1_bout));  // open: bin
  Subtractor #(.width(1)) subtractor_2 (
    .a(1'b0), .b(and_2_out), .out(subtractor_1_out[1]), .bin(subtractor_1_bout), .bout(subtractor_2_bout));
  Subtractor #(.width(1)) subtractor_3 (
    .a(1'b1), .b(and_3_out), .out(subtractor_1_out[2]), .bin(subtractor_2_bout), .bout(subtractor_3_bout));
  Subtractor #(.width(1)) subtractor_4 (
    .a(1'b1), .b(and_4_out), .out(subtractor_1_out[3]), .bin(subtractor_3_bout), .bout(subtractor_4_bout));
  Subtractor #(.width(1)) subtractor_5 (
    .a(1'b0), .b(and_5_out), .out(subtractor_1_out[4]), .bin(subtractor_4_bout), .bout(subtractor_5_bout));
  Subtractor #(.width(1)) subtractor_6 (
    .a(1'b0), .b(and_6_out), .out(subtractor_1_out[5]), .bin(subtractor_5_bout), .bout(subtractor_6_bout));
  Subtractor #(.width(1)) subtractor_7 (
    .a(1'b0), .b(and_7_out), .out(subtractor_1_out[6]), .bin(subtractor_6_bout), .bout(subtractor_7_bout));
  Subtractor #(.width(1)) subtractor_8 (
    .a(1'b0), .b(and_8_out), .out(subtractor_1_out[7]), .bin(subtractor_7_bout));  // open: bout
  assign bit_extender_3_out = {{6{1'b0}}, subtractor_1_out};  // Bit_Extender bit_extender_3
  Shifter #(.width(14)) shifter_2 (.in(bit_extender_4_out), .\dist (4'b0110), .out(shifter_2_out));
  Pull_Resistor pull_resistor_9 (.node(pull_resistor_9_node));
  and and_9 (and_9_out, pull_resistor_9_node, not_2_out);
  Pull_Resistor pull_resistor_10 (.node(pull_resistor_10_node));
  and and_10 (and_10_out, pull_resistor_10_node, not_2_out);
  Pull_Resistor pull_resistor_11 (.node(pull_resistor_11_node));
  and and_11 (and_11_out, pull_resistor_11_node, not_2_out);
  Pull_Resistor pull_resistor_12 (.node(pull_resistor_12_node));
  and and_12 (and_12_out, pull_resistor_12_node, not_2_out);
  Pull_Resistor pull_resistor_13 (.node(pull_resistor_13_node));
  and and_13 (and_13_out, pull_resistor_13_node, not_2_out);
  Pull_Resistor pull_resistor_14 (.node(pull_resistor_14_node));
  and and_14 (and_14_out, pull_resistor_14_node, not_2_out);
  Pull_Resistor pull_resistor_15 (.node(pull_resistor_8_node[0]));
  and and_15 (and_15_out, pull_resistor_8_node[0], not_2_out);
  Pull_Resistor pull_resistor_16 (.node(pull_resistor_8_node[1]));
  and and_16 (and_16_out, pull_resistor_8_node[1], not_2_out);
  assign bit_extender_4_out = {{6{1'b0}}, {1'b0, pull_resistor_8_node}};  // Bit_Extender bit_extender_4
  not not_2 (not_2_out, comparator_2_gt);
  Comparator #(.width(14), .mode("unsigned")) comparator_2 (
    .a(shifter_2_out), .b(bit_extender_3_out), .gt(comparator_2_gt));  // open: eq, lt
  Subtractor #(.width(1)) subtractor_9 (
    .a(subtractor_1_out[0]), .b(and_9_out), .out(subtractor_9_out[0]), .bout(subtractor_9_bout));  // open: bin
  Subtractor #(.width(1)) subtractor_10 (
    .a(subtractor_1_out[1]), .b(and_10_out), .out(subtractor_9_out[1]), .bin(subtractor_9_bout),
    .bout(subtractor_10_bout));
  Subtractor #(.width(1)) subtractor_11 (
    .a(subtractor_1_out[2]), .b(and_11_out), .out(subtractor_9_out[2]), .bin(subtractor_10_bout),
    .bout(subtractor_11_bout));
  Subtractor #(.width(1)) subtractor_12 (
    .a(subtractor_1_out[3]), .b(and_12_out), .out(subtractor_9_out[3]), .bin(subtractor_11_bout),
    .bout(subtractor_12_bout));
  Subtractor #(.width(1)) subtractor_13 (
    .a(subtractor_1_out[4]), .b(and_13_out), .out(subtractor_9_out[4]), .bin(subtractor_12_bout),
    .bout(subtractor_13_bout));
  Subtractor #(.width(1)) subtractor_14 (
    .a(subtractor_1_out[5]), .b(and_14_out), .out(subtractor_9_out[5]), .bin(subtractor_13_bout),
    .bout(subtractor_14_bout));
  Subtractor #(.width(1)) subtractor_15 (
    .a(subtractor_1_out[6]), .b(and_15_out), .out(subtractor_9_out[6]), .bin(subtractor_14_bout),
    .bout(subtractor_15_bout));
  Subtractor #(.width(1)) subtractor_16 (
    .a(subtractor_1_out[7]), .b(and_16_out), .out(subtractor_9_out[7]), .bin(subtractor_15_bout));  // open: bout
  assign bit_extender_5_out = {{5{1'b0}}, subtractor_9_out};  // Bit_Extender bit_extender_5
  Shifter #(.width(13)) shifter_3 (.in(bit_extender_6_out), .\dist (4'b0101), .out(shifter_3_out));
  Pull_Resistor pull_resistor_17 (.node(pull_resistor_17_node));
  and and_17 (and_17_out, pull_resistor_17_node, not_3_out);
  Pull_Resistor pull_resistor_18 (.node(pull_resistor_18_node));
  and and_18 (and_18_out, pull_resistor_18_node, not_3_out);
  Pull_Resistor pull_resistor_19 (.node(pull_resistor_19_node));
  and and_19 (and_19_out, pull_resistor_19_node, not_3_out);
  Pull_Resistor pull_resistor_20 (.node(pull_resistor_20_node));
  and and_20 (and_20_out, pull_resistor_20_node, not_3_out);
  Pull_Resistor pull_resistor_21 (.node(pull_resistor_21_node));
  and and_21 (and_21_out, pull_resistor_21_node, not_3_out);
  Pull_Resistor pull_resistor_22 (.node(pull_resistor_8_node[0]));
  and and_22 (and_22_out, pull_resistor_8_node[0], not_3_out);
  Pull_Resistor pull_resistor_23 (.node(pull_resistor_8_node[1]));
  and and_23 (and_23_out, pull_resistor_8_node[1], not_3_out);
  Pull_Resistor pull_resistor_24 (.node(pull_resistor_8_node[2]));
  and and_24 (and_24_out, pull_resistor_8_node[2], not_3_out);
  assign bit_extender_6_out = {{5{1'b0}}, {1'b0, pull_resistor_8_node}};  // Bit_Extender bit_extender_6
  not not_3 (not_3_out, comparator_3_gt);
  Comparator #(.width(13), .mode("unsigned")) comparator_3 (
    .a(shifter_3_out), .b(bit_extender_5_out), .gt(comparator_3_gt));  // open: eq, lt
  Subtractor #(.width(1)) subtractor_17 (
    .a(subtractor_9_out[0]), .b(and_17_out), .out(subtractor_17_out[0]), .bout(subtractor_17_bout));  // open: bin
  Subtractor #(.width(1)) subtractor_18 (
    .a(subtractor_9_out[1]), .b(and_18_out), .out(subtractor_17_out[1]), .bin(subtractor_17_bout),
    .bout(subtractor_18_bout));
  Subtractor #(.width(1)) subtractor_19 (
    .a(subtractor_9_out[2]), .b(and_19_out), .out(subtractor_17_out[2]), .bin(subtractor_18_bout),
    .bout(subtractor_19_bout));
  Subtractor #(.width(1)) subtractor_20 (
    .a(subtractor_9_out[3]), .b(and_20_out), .out(subtractor_17_out[3]), .bin(subtractor_19_bout),
    .bout(subtractor_20_bout));
  Subtractor #(.width(1)) subtractor_21 (
    .a(subtractor_9_out[4]), .b(and_21_out), .out(subtractor_17_out[4]), .bin(subtractor_20_bout),
    .bout(subtractor_21_bout));
  Subtractor #(.width(1)) subtractor_22 (
    .a(subtractor_9_out[5]), .b(and_22_out), .out(subtractor_17_out[5]), .bin(subtractor_21_bout),
    .bout(subtractor_22_bout));
  Subtractor #(.width(1)) subtractor_23 (
    .a(subtractor_9_out[6]), .b(and_23_out), .out(subtractor_17_out[6]), .bin(subtractor_22_bout),
    .bout(subtractor_23_bout));
  Subtractor #(.width(1)) subtractor_24 (
    .a(subtractor_9_out[7]), .b(and_24_out), .out(subtractor_17_out[7]), .bin(subtractor_23_bout));  // open: bout
  assign bit_extender_7_out = {{4{1'b0}}, subtractor_17_out};  // Bit_Extender bit_extender_7
  Shifter #(.width(12)) shifter_4 (.in(bit_extender_8_out), .\dist (4'b0100), .out(shifter_4_out));
  Pull_Resistor pull_resistor_25 (.node(pull_resistor_25_node));
  and and_25 (and_25_out, pull_resistor_25_node, not_4_out);
  Pull_Resistor pull_resistor_26 (.node(pull_resistor_26_node));
  and and_26 (and_26_out, pull_resistor_26_node, not_4_out);
  Pull_Resistor pull_resistor_27 (.node(pull_resistor_27_node));
  and and_27 (and_27_out, pull_resistor_27_node, not_4_out);
  Pull_Resistor pull_resistor_28 (.node(pull_resistor_28_node));
  and and_28 (and_28_out, pull_resistor_28_node, not_4_out);
  Pull_Resistor pull_resistor_29 (.node(pull_resistor_8_node[0]));
  and and_29 (and_29_out, pull_resistor_8_node[0], not_4_out);
  Pull_Resistor pull_resistor_30 (.node(pull_resistor_8_node[1]));
  and and_30 (and_30_out, pull_resistor_8_node[1], not_4_out);
  Pull_Resistor pull_resistor_31 (.node(pull_resistor_8_node[2]));
  and and_31 (and_31_out, pull_resistor_8_node[2], not_4_out);
  Pull_Resistor pull_resistor_32 (.node(pull_resistor_8_node[3]));
  and and_32 (and_32_out, pull_resistor_8_node[3], not_4_out);
  assign bit_extender_8_out = {{4{1'b0}}, {1'b0, pull_resistor_8_node}};  // Bit_Extender bit_extender_8
  not not_4 (not_4_out, comparator_4_gt);
  Comparator #(.width(12), .mode("unsigned")) comparator_4 (
    .a(shifter_4_out), .b(bit_extender_7_out), .gt(comparator_4_gt));  // open: eq, lt
  Subtractor #(.width(1)) subtractor_25 (
    .a(subtractor_17_out[0]), .b(and_25_out), .out(subtractor_25_out[0]), .bout(subtractor_25_bout));  // open: bin
  Subtractor #(.width(1)) subtractor_26 (
    .a(subtractor_17_out[1]), .b(and_26_out), .out(subtractor_25_out[1]), .bin(subtractor_25_bout),
    .bout(subtractor_26_bout));
  Subtractor #(.width(1)) subtractor_27 (
    .a(subtractor_17_out[2]), .b(and_27_out), .out(subtractor_25_out[2]), .bin(subtractor_26_bout),
    .bout(subtractor_27_bout));
  Subtractor #(.width(1)) subtractor_28 (
    .a(subtractor_17_out[3]), .b(and_28_out), .out(subtractor_25_out[3]), .bin(subtractor_27_bout),
    .bout(subtractor_28_bout));
  Subtractor #(.width(1)) subtractor_29 (
    .a(subtractor_17_out[4]), .b(and_29_out), .out(subtractor_25_out[4]), .bin(subtractor_28_bout),
    .bout(subtractor_29_bout));
  Subtractor #(.width(1)) subtractor_30 (
    .a(subtractor_17_out[5]), .b(and_30_out), .out(subtractor_25_out[5]), .bin(subtractor_29_bout),
    .bout(subtractor_30_bout));
  Subtractor #(.width(1)) subtractor_31 (
    .a(subtractor_17_out[6]), .b(and_31_out), .out(subtractor_25_out[6]), .bin(subtractor_30_bout),
    .bout(subtractor_31_bout));
  Subtractor #(.width(1)) subtractor_32 (
    .a(subtractor_17_out[7]), .b(and_32_out), .out(subtractor_25_out[7]), .bin(subtractor_31_bout));  // open: bout
  assign bit_extender_9_out = {{3{1'b0}}, subtractor_25_out};  // Bit_Extender bit_extender_9
  Shifter #(.width(11)) shifter_5 (.in(bit_extender_10_out), .\dist (4'b0011), .out(shifter_5_out));
  Pull_Resistor pull_resistor_33 (.node(pull_resistor_33_node));
  and and_33 (and_33_out, pull_resistor_33_node, not_5_out);
  Pull_Resistor pull_resistor_34 (.node(pull_resistor_34_node));
  and and_34 (and_34_out, pull_resistor_34_node, not_5_out);
  Pull_Resistor pull_resistor_35 (.node(pull_resistor_35_node));
  and and_35 (and_35_out, pull_resistor_35_node, not_5_out);
  Pull_Resistor pull_resistor_36 (.node(pull_resistor_8_node[0]));
  and and_36 (and_36_out, pull_resistor_8_node[0], not_5_out);
  Pull_Resistor pull_resistor_37 (.node(pull_resistor_8_node[1]));
  and and_37 (and_37_out, pull_resistor_8_node[1], not_5_out);
  Pull_Resistor pull_resistor_38 (.node(pull_resistor_8_node[2]));
  and and_38 (and_38_out, pull_resistor_8_node[2], not_5_out);
  Pull_Resistor pull_resistor_39 (.node(pull_resistor_8_node[3]));
  and and_39 (and_39_out, pull_resistor_8_node[3], not_5_out);
  Pull_Resistor pull_resistor_40 (.node(pull_resistor_8_node[4]));
  and and_40 (and_40_out, pull_resistor_8_node[4], not_5_out);
  assign bit_extender_10_out = {{3{1'b0}}, {1'b0, pull_resistor_8_node}};  // Bit_Extender bit_extender_10
  not not_5 (not_5_out, comparator_5_gt);
  Comparator #(.width(11), .mode("unsigned")) comparator_5 (
    .a(shifter_5_out), .b(bit_extender_9_out), .gt(comparator_5_gt));  // open: eq, lt
  Subtractor #(.width(1)) subtractor_33 (
    .a(subtractor_25_out[0]), .b(and_33_out), .out(subtractor_33_out[0]), .bout(subtractor_33_bout));  // open: bin
  Subtractor #(.width(1)) subtractor_34 (
    .a(subtractor_25_out[1]), .b(and_34_out), .out(subtractor_33_out[1]), .bin(subtractor_33_bout),
    .bout(subtractor_34_bout));
  Subtractor #(.width(1)) subtractor_35 (
    .a(subtractor_25_out[2]), .b(and_35_out), .out(subtractor_33_out[2]), .bin(subtractor_34_bout),
    .bout(subtractor_35_bout));
  Subtractor #(.width(1)) subtractor_36 (
    .a(subtractor_25_out[3]), .b(and_36_out), .out(subtractor_33_out[3]), .bin(subtractor_35_bout),
    .bout(subtractor_36_bout));
  Subtractor #(.width(1)) subtractor_37 (
    .a(subtractor_25_out[4]), .b(and_37_out), .out(subtractor_33_out[4]), .bin(subtractor_36_bout),
    .bout(subtractor_37_bout));
  Subtractor #(.width(1)) subtractor_38 (
    .a(subtractor_25_out[5]), .b(and_38_out), .out(subtractor_33_out[5]), .bin(subtractor_37_bout),
    .bout(subtractor_38_bout));
  Subtractor #(.width(1)) subtractor_39 (
    .a(subtractor_25_out[6]), .b(and_39_out), .out(subtractor_33_out[6]), .bin(subtractor_38_bout),
    .bout(subtractor_39_bout));
  Subtractor #(.width(1)) subtractor_40 (
    .a(subtractor_25_out[7]), .b(and_40_out), .out(subtractor_33_out[7]), .bin(subtractor_39_bout));  // open: bout
  assign bit_extender_11_out = {{2{1'b0}}, subtractor_33_out};  // Bit_Extender bit_extender_11
  Shifter #(.width(10)) shifter_6 (.in(bit_extender_12_out), .\dist (4'b0010), .out(shifter_6_out));
  Pull_Resistor pull_resistor_41 (.node(pull_resistor_41_node));
  and and_41 (and_41_out, pull_resistor_41_node, not_6_out);
  Pull_Resistor pull_resistor_42 (.node(pull_resistor_42_node));
  and and_42 (and_42_out, pull_resistor_42_node, not_6_out);
  Pull_Resistor pull_resistor_43 (.node(pull_resistor_8_node[0]));
  and and_43 (and_43_out, pull_resistor_8_node[0], not_6_out);
  Pull_Resistor pull_resistor_44 (.node(pull_resistor_8_node[1]));
  and and_44 (and_44_out, pull_resistor_8_node[1], not_6_out);
  Pull_Resistor pull_resistor_45 (.node(pull_resistor_8_node[2]));
  and and_45 (and_45_out, pull_resistor_8_node[2], not_6_out);
  Pull_Resistor pull_resistor_46 (.node(pull_resistor_8_node[3]));
  and and_46 (and_46_out, pull_resistor_8_node[3], not_6_out);
  Pull_Resistor pull_resistor_47 (.node(pull_resistor_8_node[4]));
  and and_47 (and_47_out, pull_resistor_8_node[4], not_6_out);
  Pull_Resistor pull_resistor_48 (.node(pull_resistor_8_node[5]));
  and and_48 (and_48_out, pull_resistor_8_node[5], not_6_out);
  assign bit_extender_12_out = {{2{1'b0}}, {1'b0, pull_resistor_8_node}};  // Bit_Extender bit_extender_12
  not not_6 (not_6_out, comparator_6_gt);
  Comparator #(.width(10), .mode("unsigned")) comparator_6 (
    .a(shifter_6_out), .b(bit_extender_11_out), .gt(comparator_6_gt));  // open: eq, lt
  Subtractor #(.width(1)) subtractor_41 (
    .a(subtractor_33_out[0]), .b(and_41_out), .out(subtractor_41_out[0]), .bout(subtractor_41_bout));  // open: bin
  Subtractor #(.width(1)) subtractor_42 (
    .a(subtractor_33_out[1]), .b(and_42_out), .out(subtractor_41_out[1]), .bin(subtractor_41_bout),
    .bout(subtractor_42_bout));
  Subtractor #(.width(1)) subtractor_43 (
    .a(subtractor_33_out[2]), .b(and_43_out), .out(subtractor_41_out[2]), .bin(subtractor_42_bout),
    .bout(subtractor_43_bout));
  Subtractor #(.width(1)) subtractor_44 (
    .a(subtractor_33_out[3]), .b(and_44_out), .out(subtractor_41_out[3]), .bin(subtractor_43_bout),
    .bout(subtractor_44_bout));
  Subtractor #(.width(1)) subtractor_45 (
    .a(subtractor_33_out[4]), .b(and_45_out), .out(subtractor_41_out[4]), .bin(subtractor_44_bout),
    .bout(subtractor_45_bout));
  Subtractor #(.width(1)) subtractor_46 (
    .a(subtractor_33_out[5]), .b(and_46_out), .out(subtractor_41_out[5]), .bin(subtractor_45_bout),
    .bout(subtractor_46_bout));
  Subtractor #(.width(1)) subtractor_47 (
    .a(subtractor_33_out[6]), .b(and_47_out), .out(subtractor_41_out[6]), .bin(subtractor_46_bout),
    .bout(subtractor_47_bout));
  Subtractor #(.width(1)) subtractor_48 (
    .a(subtractor_33_out[7]), .b(and_48_out), .out(subtractor_41_out[7]), .bin(subtractor_47_bout));  // open: bout
  assign bit_extender_13_out = {{1{1'b0}}, subtractor_41_out};  // Bit_Extender bit_extender_13
  Shifter #(.width(9)) shifter_7 (.in(bit_extender_14_out), .\dist (4'b0001), .out(shifter_7_out));
  Pull_Resistor pull_resistor_49 (.node(pull_resistor_49_node));
  and and_49 (and_49_out, pull_resistor_49_node, not_7_out);
  Pull_Resistor pull_resistor_50 (.node(pull_resistor_8_node[0]));
  and and_50 (and_50_out, pull_resistor_8_node[0], not_7_out);
  Pull_Resistor pull_resistor_51 (.node(pull_resistor_8_node[1]));
  and and_51 (and_51_out, pull_resistor_8_node[1], not_7_out);
  Pull_Resistor pull_resistor_52 (.node(pull_resistor_8_node[2]));
  and and_52 (and_52_out, pull_resistor_8_node[2], not_7_out);
  Pull_Resistor pull_resistor_53 (.node(pull_resistor_8_node[3]));
  and and_53 (and_53_out, pull_resistor_8_node[3], not_7_out);
  Pull_Resistor pull_resistor_54 (.node(pull_resistor_8_node[4]));
  and and_54 (and_54_out, pull_resistor_8_node[4], not_7_out);
  Pull_Resistor pull_resistor_55 (.node(pull_resistor_8_node[5]));
  and and_55 (and_55_out, pull_resistor_8_node[5], not_7_out);
  Pull_Resistor pull_resistor_56 (.node(pull_resistor_8_node[6]));
  and and_56 (and_56_out, pull_resistor_8_node[6], not_7_out);
  assign bit_extender_14_out = {{1{1'b0}}, {1'b0, pull_resistor_8_node}};  // Bit_Extender bit_extender_14
  not not_7 (not_7_out, comparator_7_gt);
  Comparator #(.width(9), .mode("unsigned")) comparator_7 (
    .a(shifter_7_out), .b(bit_extender_13_out), .gt(comparator_7_gt));  // open: eq, lt
  Subtractor #(.width(1)) subtractor_49 (
    .a(subtractor_41_out[0]), .b(and_49_out), .out(subtractor_49_out[0]), .bout(subtractor_49_bout));  // open: bin
  Subtractor #(.width(1)) subtractor_50 (
    .a(subtractor_41_out[1]), .b(and_50_out), .out(subtractor_49_out[1]), .bin(subtractor_49_bout),
    .bout(subtractor_50_bout));
  Subtractor #(.width(1)) subtractor_51 (
    .a(subtractor_41_out[2]), .b(and_51_out), .out(subtractor_49_out[2]), .bin(subtractor_50_bout),
    .bout(subtractor_51_bout));
  Subtractor #(.width(1)) subtractor_52 (
    .a(subtractor_41_out[3]), .b(and_52_out), .out(subtractor_49_out[3]), .bin(subtractor_51_bout),
    .bout(subtractor_52_bout));
  Subtractor #(.width(1)) subtractor_53 (
    .a(subtractor_41_out[4]), .b(and_53_out), .out(subtractor_49_out[4]), .bin(subtractor_52_bout),
    .bout(subtractor_53_bout));
  Subtractor #(.width(1)) subtractor_54 (
    .a(subtractor_41_out[5]), .b(and_54_out), .out(subtractor_49_out[5]), .bin(subtractor_53_bout),
    .bout(subtractor_54_bout));
  Subtractor #(.width(1)) subtractor_55 (
    .a(subtractor_41_out[6]), .b(and_55_out), .out(subtractor_49_out[6]), .bin(subtractor_54_bout),
    .bout(subtractor_55_bout));
  Subtractor #(.width(1)) subtractor_56 (
    .a(subtractor_41_out[7]), .b(and_56_out), .out(subtractor_49_out[7]), .bin(subtractor_55_bout));  // open: bout
  and and_57 (and_57_out, pull_resistor_8_node[0], not_8_out);
  and and_58 (and_58_out, pull_resistor_8_node[1], not_8_out);
  and and_59 (and_59_out, pull_resistor_8_node[2], not_8_out);
  and and_60 (and_60_out, pull_resistor_8_node[3], not_8_out);
  and and_61 (and_61_out, pull_resistor_8_node[4], not_8_out);
  and and_62 (and_62_out, pull_resistor_8_node[5], not_8_out);
  and and_63 (and_63_out, pull_resistor_8_node[6], not_8_out);
  and and_64 (and_64_out, 1'b0, not_8_out);
  not not_8 (not_8_out, comparator_8_gt);
  Comparator #(.mode("unsigned")) comparator_8 (
    .a({1'b0, pull_resistor_8_node}), .b(subtractor_49_out), .gt(comparator_8_gt));  // open: eq, lt
  Subtractor #(.width(1)) subtractor_57 (
    .a(subtractor_49_out[0]), .b(and_57_out), .out(subtractor_57_out), .bout(subtractor_57_bout));  // open: bin
  Subtractor #(.width(1)) subtractor_58 (
    .a(subtractor_49_out[1]), .b(and_58_out), .out(subtractor_58_out), .bin(subtractor_57_bout),
    .bout(subtractor_58_bout));
  Subtractor #(.width(1)) subtractor_59 (
    .a(subtractor_49_out[2]), .b(and_59_out), .out(subtractor_59_out), .bin(subtractor_58_bout),
    .bout(subtractor_59_bout));
  Subtractor #(.width(1)) subtractor_60 (
    .a(subtractor_49_out[3]), .b(and_60_out), .out(subtractor_60_out), .bin(subtractor_59_bout),
    .bout(subtractor_60_bout));
  Subtractor #(.width(1)) subtractor_61 (
    .a(subtractor_49_out[4]), .b(and_61_out), .out(subtractor_61_out), .bin(subtractor_60_bout),
    .bout(subtractor_61_bout));
  Subtractor #(.width(1)) subtractor_62 (
    .a(subtractor_49_out[5]), .b(and_62_out), .out(subtractor_62_out), .bin(subtractor_61_bout),
    .bout(subtractor_62_bout));
  Subtractor #(.width(1)) subtractor_63 (
    .a(subtractor_49_out[6]), .b(and_63_out), .out(subtractor_63_out), .bin(subtractor_62_bout),
    .bout(subtractor_63_bout));
  Subtractor #(.width(1)) subtractor_64 (
    .a(subtractor_49_out[7]), .b(and_64_out), .out(subtractor_64_out), .bin(subtractor_63_bout));  // open: bout
  // also tied to GND on the sheet: {pull_resistor_8_node[0], pull_resistor_8_node[2], pull_resistor_8_node[3], pull_resistor_8_node[4], pull_resistor_8_node[5], pull_resistor_8_node[6]}
  // also tied to VCC on the sheet: pull_resistor_8_node[1]

  // Notes on the sheet:
  //   Dividend
  //   Divisor
  //   Result
  //   Remainder
endmodule

module gate_memory (
);

  wire button_1_out, button_2_out, not_1_out, not_2_out, or_1_out, or_2_out;

  Button button_1 (.out(button_1_out));
  or or_1 (or_1_out, button_1_out, not_2_out);
  or or_2 (or_2_out, not_1_out, button_2_out);
  not not_1 (not_1_out, or_1_out);
  LED led_1 (.in(not_1_out));
  LED led_2 (.in(not_2_out));
  not not_2 (not_2_out, or_2_out);
  Button button_2 (.out(button_2_out));
endmodule

module multiplier (
);

  wire adder_1_cout, adder_1_out, adder_2_cout, adder_2_out, adder_3_cout, adder_3_out, adder_4_cout,
       adder_4_out, adder_5_cout, adder_5_out, adder_6_cout, adder_6_out, adder_7_cout, adder_7_out,
       adder_8_cout, adder_8_out, adder_9_cout, adder_9_out, adder_10_cout, adder_10_out, adder_11_cout,
       adder_11_out, adder_12_cout, adder_12_out, adder_13_cout, adder_13_out, adder_14_cout, adder_14_out,
       adder_15_cout, adder_15_out, adder_16_cout, adder_16_out, adder_17_cout, adder_17_out, adder_18_cout,
       adder_18_out, adder_19_cout, adder_19_out, adder_20_cout, adder_20_out, adder_21_cout, adder_21_out,
       adder_22_cout, adder_22_out, adder_23_cout, adder_23_out, adder_24_cout, adder_24_out, adder_25_cout,
       adder_25_out, adder_26_cout, adder_26_out, adder_27_cout, adder_27_out, adder_28_cout, adder_28_out,
       adder_29_cout, adder_29_out, adder_30_cout, adder_30_out, adder_31_cout, adder_31_out, adder_32_cout,
       adder_32_out, adder_33_cout, adder_33_out, adder_34_cout, adder_34_out, adder_35_cout, adder_35_out,
       adder_36_cout, adder_36_out, adder_37_cout, adder_37_out, adder_38_cout, adder_38_out, adder_39_cout,
       adder_39_out, adder_40_cout, adder_40_out, adder_41_cout, adder_41_out, adder_42_cout, adder_42_out,
       adder_43_cout, adder_43_out, adder_44_cout, adder_44_out, adder_45_cout, adder_45_out, adder_46_cout,
       adder_46_out, adder_47_cout, adder_47_out, adder_48_cout, adder_48_out, adder_49_cout, adder_49_out,
       adder_50_cout, adder_50_out, adder_51_cout, adder_51_out, adder_52_cout, adder_52_out, adder_53_cout,
       adder_53_out, adder_54_cout, adder_54_out, adder_55_cout, adder_55_out, adder_56_cout, adder_56_out,
       and_1_out, and_2_out, and_3_out, and_4_out, and_5_out, and_6_out, and_7_out, and_8_out, and_9_out,
       and_10_out, and_11_out, and_12_out, and_13_out, and_14_out, and_15_out, and_16_out, and_17_out,
       and_18_out, and_19_out, and_20_out, and_21_out, and_22_out, and_23_out, and_24_out, and_25_out,
       and_26_out, and_27_out, and_28_out, and_29_out, and_30_out, and_31_out, and_32_out, and_33_out,
       and_34_out, and_35_out, and_36_out, and_37_out, and_38_out, and_39_out, and_40_out, and_41_out,
       and_42_out, and_43_out, and_44_out, and_45_out, and_46_out, and_47_out, and_48_out, and_49_out,
       and_50_out, and_51_out, and_52_out, and_53_out, and_54_out, and_55_out, and_56_out, and_57_out,
       and_58_out, and_59_out, and_60_out, and_61_out, and_62_out, and_63_out, and_64_out;

  and and_1 (and_1_out, 1'b1, 1'b1);
  and and_2 (and_2_out, 1'b1, 1'b1);
  and and_3 (and_3_out, 1'b1, 1'b1);
  and and_4 (and_4_out, 1'b0, 1'b1);
  and and_5 (and_5_out, 1'b1, 1'b1);
  and and_6 (and_6_out, 1'b0, 1'b1);
  and and_7 (and_7_out, 1'b0, 1'b1);
  and and_8 (and_8_out, 1'b0, 1'b1);
  and and_9 (and_9_out, 1'b1, 1'b1);
  Adder #(.width(1)) adder_1 (.a(and_9_out), .b(and_2_out), .out(adder_1_out), .cout(adder_1_cout));  // open: cin
  and and_10 (and_10_out, 1'b1, 1'b1);
  Adder #(.width(1)) adder_2 (
    .a(and_10_out), .b(and_3_out), .out(adder_2_out), .cin(adder_1_cout), .cout(adder_2_cout));
  and and_11 (and_11_out, 1'b1, 1'b1);
  Adder #(.width(1)) adder_3 (
    .a(and_11_out), .b(and_4_out), .out(adder_3_out), .cin(adder_2_cout), .cout(adder_3_cout));
  and and_12 (and_12_out, 1'b0, 1'b1);
  Adder #(.width(1)) adder_4 (
    .a(and_12_out), .b(and_5_out), .out(adder_4_out), .cin(adder_3_cout), .cout(adder_4_cout));
  and and_13 (and_13_out, 1'b1, 1'b1);
  Adder #(.width(1)) adder_5 (
    .a(and_13_out), .b(and_6_out), .out(adder_5_out), .cin(adder_4_cout), .cout(adder_5_cout));
  and and_14 (and_14_out, 1'b0, 1'b1);
  Adder #(.width(1)) adder_6 (
    .a(and_14_out), .b(and_7_out), .out(adder_6_out), .cin(adder_5_cout), .cout(adder_6_cout));
  and and_15 (and_15_out, 1'b0, 1'b1);
  Adder #(.width(1)) adder_7 (
    .a(and_15_out), .b(and_8_out), .out(adder_7_out), .cin(adder_6_cout), .cout(adder_7_cout));
  and and_16 (and_16_out, 1'b0, 1'b1);
  Adder #(.width(1)) adder_8 (.a(and_16_out), .b(1'b0), .out(adder_8_out), .cin(adder_7_cout), .cout(adder_8_cout));
  and and_17 (and_17_out, 1'b1, 1'b1);
  Adder #(.width(1)) adder_9 (.a(and_17_out), .b(adder_2_out), .out(adder_9_out), .cout(adder_9_cout));  // open: cin
  and and_18 (and_18_out, 1'b1, 1'b1);
  Adder #(.width(1)) adder_10 (
    .a(and_18_out), .b(adder_3_out), .out(adder_10_out), .cin(adder_9_cout), .cout(adder_10_cout));
  and and_19 (and_19_out, 1'b1, 1'b1);
  Adder #(.width(1)) adder_11 (
    .a(and_19_out), .b(adder_4_out), .out(adder_11_out), .cin(adder_10_cout), .cout(adder_11_cout));
  and and_20 (and_20_out, 1'b0, 1'b1);
  Adder #(.width(1)) adder_12 (
    .a(and_20_out), .b(adder_5_out), .out(adder_12_out), .cin(adder_11_cout), .cout(adder_12_cout));
  and and_21 (and_21_out, 1'b1, 1'b1);
  Adder #(.width(1)) adder_13 (
    .a(and_21_out), .b(adder_6_out), .out(adder_13_out), .cin(adder_12_cout), .cout(adder_13_cout));
  and and_22 (and_22_out, 1'b0, 1'b1);
  Adder #(.width(1)) adder_14 (
    .a(and_22_out), .b(adder_7_out), .out(adder_14_out), .cin(adder_13_cout), .cout(adder_14_cout));
  and and_23 (and_23_out, 1'b0, 1'b1);
  Adder #(.width(1)) adder_15 (
    .a(and_23_out), .b(adder_8_out), .out(adder_15_out), .cin(adder_14_cout), .cout(adder_15_cout));
  and and_24 (and_24_out, 1'b0, 1'b1);
  Adder #(.width(1)) adder_16 (
    .a(and_24_out), .b(adder_8_cout), .out(adder_16_out), .cin(adder_15_cout), .cout(adder_16_cout));
  and and_25 (and_25_out, 1'b1, 1'b0);
  and and_26 (and_26_out, 1'b1, 1'b0);
  and and_27 (and_27_out, 1'b1, 1'b0);
  and and_28 (and_28_out, 1'b0, 1'b0);
  and and_29 (and_29_out, 1'b1, 1'b0);
  and and_30 (and_30_out, 1'b0, 1'b0);
  and and_31 (and_31_out, 1'b0, 1'b0);
  and and_32 (and_32_out, 1'b0, 1'b0);
  Adder #(.width(1)) adder_17 (
    .a(and_25_out), .b(adder_10_out), .out(adder_17_out), .cout(adder_17_cout));  // open: cin
  and and_33 (and_33_out, 1'b1, 1'b1);
  Adder #(.width(1)) adder_18 (
    .a(and_26_out), .b(adder_11_out), .out(adder_18_out), .cin(adder_17_cout), .cout(adder_18_cout));
  and and_34 (and_34_out, 1'b1, 1'b1);
  Adder #(.width(1)) adder_19 (
    .a(and_27_out), .b(adder_12_out), .out(adder_19_out), .cin(adder_18_cout), .cout(adder_19_cout));
  and and_35 (and_35_out, 1'b1, 1'b1);
  Adder #(.width(1)) adder_20 (
    .a(and_28_out), .b(adder_13_out), .out(adder_20_out), .cin(adder_19_cout), .cout(adder_20_cout));
  and and_36 (and_36_out, 1'b0, 1'b1);
  Adder #(.width(1)) adder_21 (
    .a(and_29_out), .b(adder_14_out), .out(adder_21_out), .cin(adder_20_cout), .cout(adder_21_cout));
  and and_37 (and_37_out, 1'b1, 1'b1);
  Adder #(.width(1)) adder_22 (
    .a(and_30_out), .b(adder_15_out), .out(adder_22_out), .cin(adder_21_cout), .cout(adder_22_cout));
  and and_38 (and_38_out, 1'b0, 1'b1);
  Adder #(.width(1)) adder_23 (
    .a(and_31_out), .b(adder_16_out), .out(adder_23_out), .cin(adder_22_cout), .cout(adder_23_cout));
  and and_39 (and_39_out, 1'b0, 1'b1);
  Adder #(.width(1)) adder_24 (
    .a(and_32_out), .b(adder_16_cout), .out(adder_24_out), .cin(adder_23_cout), .cout(adder_24_cout));
  and and_40 (and_40_out, 1'b0, 1'b1);
  Adder #(.width(1)) adder_25 (
    .a(and_33_out), .b(adder_18_out), .out(adder_25_out), .cout(adder_25_cout));  // open: cin
  and and_41 (and_41_out, 1'b1, 1'b0);
  Adder #(.width(1)) adder_26 (
    .a(and_34_out), .b(adder_19_out), .out(adder_26_out), .cin(adder_25_cout), .cout(adder_26_cout));
  and and_42 (and_42_out, 1'b1, 1'b0);
  Adder #(.width(1)) adder_27 (
    .a(and_35_out), .b(adder_20_out), .out(adder_27_out), .cin(adder_26_cout), .cout(adder_27_cout));
  and and_43 (and_43_out, 1'b1, 1'b0);
  Adder #(.width(1)) adder_28 (
    .a(and_36_out), .b(adder_21_out), .out(adder_28_out), .cin(adder_27_cout), .cout(adder_28_cout));
  and and_44 (and_44_out, 1'b0, 1'b0);
  Adder #(.width(1)) adder_29 (
    .a(and_37_out), .b(adder_22_out), .out(adder_29_out), .cin(adder_28_cout), .cout(adder_29_cout));
  and and_45 (and_45_out, 1'b1, 1'b0);
  Adder #(.width(1)) adder_30 (
    .a(and_38_out), .b(adder_23_out), .out(adder_30_out), .cin(adder_29_cout), .cout(adder_30_cout));
  and and_46 (and_46_out, 1'b0, 1'b0);
  Adder #(.width(1)) adder_31 (
    .a(and_39_out), .b(adder_24_out), .out(adder_31_out), .cin(adder_30_cout), .cout(adder_31_cout));
  and and_47 (and_47_out, 1'b0, 1'b0);
  Adder #(.width(1)) adder_32 (
    .a(and_40_out), .b(adder_24_cout), .out(adder_32_out), .cin(adder_31_cout), .cout(adder_32_cout));
  and and_48 (and_48_out, 1'b0, 1'b0);
  Adder #(.width(1)) adder_33 (
    .a(and_41_out), .b(adder_26_out), .out(adder_33_out), .cout(adder_33_cout));  // open: cin
  and and_49 (and_49_out, 1'b1, 1'b0);
  Adder #(.width(1)) adder_34 (
    .a(and_42_out), .b(adder_27_out), .out(adder_34_out), .cin(adder_33_cout), .cout(adder_34_cout));
  and and_50 (and_50_out, 1'b1, 1'b0);
  Adder #(.width(1)) adder_35 (
    .a(and_43_out), .b(adder_28_out), .out(adder_35_out), .cin(adder_34_cout), .cout(adder_35_cout));
  and and_51 (and_51_out, 1'b1, 1'b0);
  Adder #(.width(1)) adder_36 (
    .a(and_44_out), .b(adder_29_out), .out(adder_36_out), .cin(adder_35_cout), .cout(adder_36_cout));
  and and_52 (and_52_out, 1'b0, 1'b0);
  Adder #(.width(1)) adder_37 (
    .a(and_45_out), .b(adder_30_out), .out(adder_37_out), .cin(adder_36_cout), .cout(adder_37_cout));
  and and_53 (and_53_out, 1'b1, 1'b0);
  Adder #(.width(1)) adder_38 (
    .a(and_46_out), .b(adder_31_out), .out(adder_38_out), .cin(adder_37_cout), .cout(adder_38_cout));
  and and_54 (and_54_out, 1'b0, 1'b0);
  Adder #(.width(1)) adder_39 (
    .a(and_47_out), .b(adder_32_out), .out(adder_39_out), .cin(adder_38_cout), .cout(adder_39_cout));
  and and_55 (and_55_out, 1'b0, 1'b0);
  Adder #(.width(1)) adder_40 (
    .a(and_48_out), .b(adder_32_cout), .out(adder_40_out), .cin(adder_39_cout), .cout(adder_40_cout));
  and and_56 (and_56_out, 1'b0, 1'b0);
  Adder #(.width(1)) adder_41 (
    .a(and_49_out), .b(adder_34_out), .out(adder_41_out), .cout(adder_41_cout));  // open: cin
  Adder #(.width(1)) adder_42 (
    .a(and_50_out), .b(adder_35_out), .out(adder_42_out), .cin(adder_41_cout), .cout(adder_42_cout));
  Adder #(.width(1)) adder_43 (
    .a(and_51_out), .b(adder_36_out), .out(adder_43_out), .cin(adder_42_cout), .cout(adder_43_cout));
  Adder #(.width(1)) adder_44 (
    .a(and_52_out), .b(adder_37_out), .out(adder_44_out), .cin(adder_43_cout), .cout(adder_44_cout));
  Adder #(.width(1)) adder_45 (
    .a(and_53_out), .b(adder_38_out), .out(adder_45_out), .cin(adder_44_cout), .cout(adder_45_cout));
  Adder #(.width(1)) adder_46 (
    .a(and_54_out), .b(adder_39_out), .out(adder_46_out), .cin(adder_45_cout), .cout(adder_46_cout));
  Adder #(.width(1)) adder_47 (
    .a(and_55_out), .b(adder_40_out), .out(adder_47_out), .cin(adder_46_cout), .cout(adder_47_cout));
  Adder #(.width(1)) adder_48 (
    .a(and_56_out), .b(adder_40_cout), .out(adder_48_out), .cin(adder_47_cout), .cout(adder_48_cout));
  and and_57 (and_57_out, 1'b1, 1'b0);
  Adder #(.width(1)) adder_49 (
    .a(and_57_out), .b(adder_42_out), .out(adder_49_out), .cout(adder_49_cout));  // open: cin
  and and_58 (and_58_out, 1'b1, 1'b0);
  Adder #(.width(1)) adder_50 (
    .a(and_58_out), .b(adder_43_out), .out(adder_50_out), .cin(adder_49_cout), .cout(adder_50_cout));
  and and_59 (and_59_out, 1'b1, 1'b0);
  Adder #(.width(1)) adder_51 (
    .a(and_59_out), .b(adder_44_out), .out(adder_51_out), .cin(adder_50_cout), .cout(adder_51_cout));
  and and_60 (and_60_out, 1'b0, 1'b0);
  Adder #(.width(1)) adder_52 (
    .a(and_60_out), .b(adder_45_out), .out(adder_52_out), .cin(adder_51_cout), .cout(adder_52_cout));
  and and_61 (and_61_out, 1'b1, 1'b0);
  Adder #(.width(1)) adder_53 (
    .a(and_61_out), .b(adder_46_out), .out(adder_53_out), .cin(adder_52_cout), .cout(adder_53_cout));
  and and_62 (and_62_out, 1'b0, 1'b0);
  Adder #(.width(1)) adder_54 (
    .a(and_62_out), .b(adder_47_out), .out(adder_54_out), .cin(adder_53_cout), .cout(adder_54_cout));
  and and_63 (and_63_out, 1'b0, 1'b0);
  Adder #(.width(1)) adder_55 (
    .a(and_63_out), .b(adder_48_out), .out(adder_55_out), .cin(adder_54_cout), .cout(adder_55_cout));
  and and_64 (and_64_out, 1'b0, 1'b0);
  Adder #(.width(1)) adder_56 (
    .a(and_64_out), .b(adder_48_cout), .out(adder_56_out), .cin(adder_55_cout), .cout(adder_56_cout));

  // Notes on the sheet:
  //   LOW
  //   HIGH
endmodule
