// Logisim project GPU tests.circ as structural Verilog: 1 circuit, main circuit main
module main (
);

  wire and_1_out, button_1_out, clock_1_out, comparator_1_eq, gpu_core_1_clear, gpu_core_1_out_13,
       gpu_core_1_write, gpu_core_2_clear, gpu_core_2_out_13, gpu_core_2_write, gpu_core_3_clear,
       gpu_core_3_out_13, gpu_core_3_write, gpu_core_4_clear, gpu_core_4_write,
       gpu_instruction_fetcher_1_claimed__1_if_this_or_higher_unit_is_ready_to_fetch_instructions,
       gpu_instruction_fetcher_1_clock_2, gpu_instruction_fetcher_1_execute,
       gpu_instruction_fetcher_2_claimed__1_if_this_or_higher_unit_is_ready_to_fetch_instructions,
       gpu_instruction_fetcher_2_clock_2,
       gpu_instruction_fetcher_2_dat_in_use__will_output_1_if_it_or_later_unit_is_currently_fetching_instructions,
       gpu_instruction_fetcher_2_execute,
       gpu_instruction_fetcher_3_claimed__1_if_this_or_higher_unit_is_ready_to_fetch_instructions,
       gpu_instruction_fetcher_3_clock_2,
       gpu_instruction_fetcher_3_dat_in_use__will_output_1_if_it_or_later_unit_is_currently_fetching_instructions,
       gpu_instruction_fetcher_3_execute,
       gpu_instruction_fetcher_4_claimed__1_if_this_or_higher_unit_is_ready_to_fetch_instructions,
       gpu_instruction_fetcher_4_dat_in_use__will_output_1_if_it_or_later_unit_is_currently_fetching_instructions,
       gpu_instruction_fetcher_4_execute, pulse_generator_1_output;
  wire [3:0] gpu_core_1_address, gpu_core_2_address, gpu_core_3_address, gpu_core_4_address;
  wire [7:0] counter_1_q, gpu_core_1_data_2, gpu_core_2_data_2, gpu_core_3_data_2, gpu_core_4_data_2,
       gpu_instruction_fetcher_1_data_out, gpu_instruction_fetcher_1_instrution_id_out,
       gpu_instruction_fetcher_2_data_out, gpu_instruction_fetcher_2_instrution_id_out,
       gpu_instruction_fetcher_3_data_out, gpu_instruction_fetcher_3_instrution_id_out,
       gpu_instruction_fetcher_4_data_out, gpu_instruction_fetcher_4_instrution_id_out, ram_1_data;

  Counter counter_1 (
    .count(and_1_out), .Q(counter_1_q), .clk(clock_1_out), .clr(pulse_generator_1_output));  // open: load, D, carry
  Clock clock_1 (.out(clock_1_out));
  and and_1 (and_1_out, ~comparator_1_eq, gpu_instruction_fetcher_4_claimed__1_if_this_or_higher_unit_is_ready_to_fetch_instructions);  // AND_Gate
  Pulse_Generator pulse_generator_1 (
    .Input(button_1_out), .Rising_Falling__If_1__will_pulse_on_falling_edge(1'b1),
    .Output(pulse_generator_1_output));
  Button button_1 (.out(button_1_out));
  Comparator comparator_1 (.a(ram_1_data), .b({8{1'b0}}), .eq(comparator_1_eq));  // open: gt, lt
  RAM ram_1 (.addr(counter_1_q), .data(ram_1_data));  // open: sel, clk, ld, clr
  GPU_Instruction_Fetcher gpu_instruction_fetcher_1 (
    .Data_In__Enter_Number_of_commands__then_commands_in_reverse_order(ram_1_data),
    .Core_Data__Data_output_or_input(gpu_core_1_data_2), .Data_out(gpu_instruction_fetcher_1_data_out),
    .Clear__1_clears_buffers_contents(gpu_core_1_clear),
    .Core_Address__Address_for_read_or_write(gpu_core_1_address),
    .Execute(gpu_instruction_fetcher_1_execute),
    .Instrution_ID_out(gpu_instruction_fetcher_1_instrution_id_out), .Clock(clock_1_out),
    .Clock_2(gpu_instruction_fetcher_1_clock_2),
    .Dat_in_Use__If_1_unit_will_not_try_to_fetch_instructions(gpu_instruction_fetcher_2_dat_in_use__will_output_1_if_it_or_later_unit_is_currently_fetching_instructions),
    .Claimed__1_if_this_or_higher_unit_is_ready_to_fetch_Instructions(gpu_instruction_fetcher_1_claimed__1_if_this_or_higher_unit_is_ready_to_fetch_instructions),
    .Write__If_1__will_write_data__else_will_read(gpu_core_1_write));  // open: Instruction_ID_in, Dat_in_Use__Will_output_1_if_it_or_later_unit_is_currently_fetching_instructions, Ready__If_1__unit_will_not_fetch_instructions
  GPU_Instruction_Fetcher gpu_instruction_fetcher_2 (
    .Data_In__Enter_Number_of_commands__then_commands_in_reverse_order(ram_1_data),
    .Core_Data__Data_output_or_input(gpu_core_2_data_2), .Data_out(gpu_instruction_fetcher_2_data_out),
    .Clear__1_clears_buffers_contents(gpu_core_2_clear),
    .Core_Address__Address_for_read_or_write(gpu_core_2_address),
    .Execute(gpu_instruction_fetcher_2_execute),
    .Instrution_ID_out(gpu_instruction_fetcher_2_instrution_id_out),
    .Clock(gpu_instruction_fetcher_1_clock_2),
    .Dat_in_Use__Will_output_1_if_it_or_later_unit_is_currently_fetching_instructions(gpu_instruction_fetcher_2_dat_in_use__will_output_1_if_it_or_later_unit_is_currently_fetching_instructions),
    .Ready__If_1__unit_will_not_fetch_instructions(gpu_instruction_fetcher_1_claimed__1_if_this_or_higher_unit_is_ready_to_fetch_instructions),
    .Clock_2(gpu_instruction_fetcher_2_clock_2),
    .Dat_in_Use__If_1_unit_will_not_try_to_fetch_instructions(gpu_instruction_fetcher_3_dat_in_use__will_output_1_if_it_or_later_unit_is_currently_fetching_instructions),
    .Claimed__1_if_this_or_higher_unit_is_ready_to_fetch_Instructions(gpu_instruction_fetcher_2_claimed__1_if_this_or_higher_unit_is_ready_to_fetch_instructions),
    .Write__If_1__will_write_data__else_will_read(gpu_core_2_write));  // open: Instruction_ID_in
  GPU_Instruction_Fetcher gpu_instruction_fetcher_3 (
    .Data_In__Enter_Number_of_commands__then_commands_in_reverse_order(ram_1_data),
    .Core_Data__Data_output_or_input(gpu_core_3_data_2), .Data_out(gpu_instruction_fetcher_3_data_out),
    .Clear__1_clears_buffers_contents(gpu_core_3_clear),
    .Core_Address__Address_for_read_or_write(gpu_core_3_address),
    .Execute(gpu_instruction_fetcher_3_execute),
    .Instrution_ID_out(gpu_instruction_fetcher_3_instrution_id_out),
    .Clock(gpu_instruction_fetcher_2_clock_2),
    .Dat_in_Use__Will_output_1_if_it_or_later_unit_is_currently_fetching_instructions(gpu_instruction_fetcher_3_dat_in_use__will_output_1_if_it_or_later_unit_is_currently_fetching_instructions),
    .Ready__If_1__unit_will_not_fetch_instructions(gpu_instruction_fetcher_2_claimed__1_if_this_or_higher_unit_is_ready_to_fetch_instructions),
    .Clock_2(gpu_instruction_fetcher_3_clock_2),
    .Dat_in_Use__If_1_unit_will_not_try_to_fetch_instructions(gpu_instruction_fetcher_4_dat_in_use__will_output_1_if_it_or_later_unit_is_currently_fetching_instructions),
    .Claimed__1_if_this_or_higher_unit_is_ready_to_fetch_Instructions(gpu_instruction_fetcher_3_claimed__1_if_this_or_higher_unit_is_ready_to_fetch_instructions),
    .Write__If_1__will_write_data__else_will_read(gpu_core_3_write));  // open: Instruction_ID_in
  GPU_Instruction_Fetcher gpu_instruction_fetcher_4 (
    .Data_In__Enter_Number_of_commands__then_commands_in_reverse_order(ram_1_data),
    .Core_Data__Data_output_or_input(gpu_core_4_data_2), .Data_out(gpu_instruction_fetcher_4_data_out),
    .Clear__1_clears_buffers_contents(gpu_core_4_clear),
    .Core_Address__Address_for_read_or_write(gpu_core_4_address),
    .Execute(gpu_instruction_fetcher_4_execute),
    .Instrution_ID_out(gpu_instruction_fetcher_4_instrution_id_out),
    .Clock(gpu_instruction_fetcher_3_clock_2),
    .Dat_in_Use__Will_output_1_if_it_or_later_unit_is_currently_fetching_instructions(gpu_instruction_fetcher_4_dat_in_use__will_output_1_if_it_or_later_unit_is_currently_fetching_instructions),
    .Ready__If_1__unit_will_not_fetch_instructions(gpu_instruction_fetcher_3_claimed__1_if_this_or_higher_unit_is_ready_to_fetch_instructions),
    .Claimed__1_if_this_or_higher_unit_is_ready_to_fetch_Instructions(gpu_instruction_fetcher_4_claimed__1_if_this_or_higher_unit_is_ready_to_fetch_instructions),
    .Write__If_1__will_write_data__else_will_read(gpu_core_4_write));  // open: Instruction_ID_in, Clock_2, Dat_in_Use__If_1_unit_will_not_try_to_fetch_instructions
  GPU_Core gpu_core_1 (
    .Instruction_ID_in(gpu_instruction_fetcher_1_instrution_id_out), .Address(gpu_core_1_address),
    .Data_2(gpu_core_1_data_2), .Write(gpu_core_1_write), .Data(gpu_instruction_fetcher_1_data_out),
    .out_13(gpu_core_1_out_13), .Clock(clock_1_out), .Execute(gpu_instruction_fetcher_1_execute),
    .Clear(gpu_core_1_clear));  // open: Instruction_ID_out, Output, Output_Ready, Read
  GPU_Core gpu_core_2 (
    .Instruction_ID_in(gpu_instruction_fetcher_2_instrution_id_out), .Address(gpu_core_2_address),
    .Data_2(gpu_core_2_data_2), .Write(gpu_core_2_write), .Data(gpu_instruction_fetcher_2_data_out),
    .out_13(gpu_core_2_out_13), .Clock(gpu_core_1_out_13), .Execute(gpu_instruction_fetcher_2_execute),
    .Clear(gpu_core_2_clear));  // open: Instruction_ID_out, Output, Output_Ready, Read
  GPU_Core gpu_core_3 (
    .Instruction_ID_in(gpu_instruction_fetcher_3_instrution_id_out), .Address(gpu_core_3_address),
    .Data_2(gpu_core_3_data_2), .Write(gpu_core_3_write), .Data(gpu_instruction_fetcher_3_data_out),
    .out_13(gpu_core_3_out_13), .Clock(gpu_core_2_out_13), .Execute(gpu_instruction_fetcher_3_execute),
    .Clear(gpu_core_3_clear));  // open: Instruction_ID_out, Output, Output_Ready, Read
  GPU_Core gpu_core_4 (
    .Instruction_ID_in(gpu_instruction_fetcher_4_instrution_id_out), .Address(gpu_core_4_address),
    .Data_2(gpu_core_4_data_2), .Write(gpu_core_4_write), .Data(gpu_instruction_fetcher_4_data_out),
    .Clock(gpu_core_3_out_13), .Execute(gpu_instruction_fetcher_4_execute), .Clear(gpu_core_4_clear));  // open: out_13, Instruction_ID_out, Output, Output_Ready, Read
endmodule
