// Logisim project GPU.circ as structural Verilog: 2 circuits, main circuit GPU Core
module GPU_Core (
  input  [7:0] Instruction_ID_in,
  input  Read,
  input  [7:0] Data,
  input  Clock,
  input  Execute,
  output [7:0] Instruction_ID_out,
  output [7:0] Output,
  output Output_Ready,
  output Clear,
  output [3:0] Address,
  output [7:0] Data_2,
  output Write,
  output out_13
);

  wire and_1_out, and_2_out, and_3_out, and_4_out, and_5_out, and_6_out, and_7_out, and_8_out, and_9_out,
       and_10_out, and_11_out, and_12_out, and_13_out, and_14_out, and_15_out, d_ff_2_q, nor_1_out,
       not_1_out, not_2_out, not_3_out, not_4_out, or_1_out, or_2_out, or_3_out;
  wire [3:0] controlled_buffer_3_out, counter_1_q;
  wire [5:0] Macro_Counter_q;
  wire [7:0] A_q, adder_1_out, B_q, bit_extender_1_out, Clock_q, controlled_buffer_1_out,
       controlled_buffer_2_out, controlled_buffer_4_out, controlled_buffer_7_out, controlled_buffer_15_out,
       divider_1_out, multiplier_1_out, register_2_q, subtractor_1_out;
  wire [7:4] controlled_buffer_3_out_2;
  wire [7:7] comparator_1_lt;
  wire [11:0] multiplexer_1_out, multiplexer_2_out, rom_1_data, rom_2_data, rom_3_data;

  Register #(.width(4)) register_1 (.D(controlled_buffer_3_out), .Q(Address), .clk(and_1_out));  // open: en, clr
  assign bit_extender_1_out = {{4{1'b0}}, Address};  // Bit_Extender bit_extender_1
  Pull_Resistor pull_resistor_1 (.node(Data_2));
  Register A (.D(controlled_buffer_1_out), .Q(A_q), .clk(and_1_out));  // open: en, clr
  Register B (.D(controlled_buffer_2_out), .Q(B_q), .clk(and_1_out));  // open: en, clr
  Comparator comparator_1 (.a(A_q), .b(B_q), .lt(comparator_1_lt[7]));  // open: gt, eq
  Pull_Resistor pull_resistor_2 (.node(Clock));
  and and_1 (and_1_out, Clock, Execute);
  Pull_Resistor pull_resistor_3 (.node(Execute));
  not not_1 (not_1_out, Execute);
  assign controlled_buffer_1_out = multiplexer_1_out[7] ? controlled_buffer_4_out : 8'bz;  // Controlled_Buffer controlled_buffer_1
  assign controlled_buffer_2_out = multiplexer_1_out[6] ? controlled_buffer_4_out : 8'bz;  // Controlled_Buffer controlled_buffer_2
  Adder adder_1 (.a(A_q), .b(B_q), .out(adder_1_out));  // open: cin, cout
  Subtractor subtractor_1 (.a(A_q), .b(B_q), .out(subtractor_1_out));  // open: bin, bout
  Multiplier multiplier_1 (.a(A_q), .b(B_q), .out(multiplier_1_out));  // open: cin, cout
  Divider divider_1 (.a(A_q), .b(B_q), .out(divider_1_out));  // open: upper, rem
  assign {controlled_buffer_3_out_2, controlled_buffer_3_out} = multiplexer_1_out[2] ? controlled_buffer_4_out : 8'bz;  // Controlled_Buffer controlled_buffer_3
  assign controlled_buffer_4_out = multiplexer_1_out[3] ? bit_extender_1_out : 8'bz;  // Controlled_Buffer controlled_buffer_4
  assign Data_2 = Write ? controlled_buffer_4_out : 8'bz;  // Controlled_Buffer controlled_buffer_5
  assign controlled_buffer_4_out = and_8_out ? Data : 8'bz;  // Controlled_Buffer controlled_buffer_6
  and and_2 (and_2_out, not_2_out, multiplexer_1_out[11]);
  and and_3 (and_3_out, multiplexer_1_out[0], multiplexer_1_out[11]);
  assign controlled_buffer_7_out = and_12_out ? controlled_buffer_4_out : 8'bz;  // Controlled_Buffer controlled_buffer_7
  and and_4 (and_4_out, register_2_q[2], register_2_q[1], register_2_q[0]);
  or or_1 (or_1_out, not_1_out, nor_1_out);
  assign controlled_buffer_4_out = and_5_out ? adder_1_out : 8'bz;  // Controlled_Buffer controlled_buffer_8
  assign controlled_buffer_4_out = and_9_out ? subtractor_1_out : 8'bz;  // Controlled_Buffer controlled_buffer_9
  assign controlled_buffer_4_out = and_2_out ? multiplier_1_out : 8'bz;  // Controlled_Buffer controlled_buffer_10
  assign controlled_buffer_4_out = and_3_out ? divider_1_out : 8'bz;  // Controlled_Buffer controlled_buffer_11
  assign controlled_buffer_4_out = and_6_out ? A_q : 8'bz;  // Controlled_Buffer controlled_buffer_12
  assign controlled_buffer_4_out = and_10_out ? B_q : 8'bz;  // Controlled_Buffer controlled_buffer_13
  and and_5 (and_5_out, not_2_out, multiplexer_1_out[10]);
  and and_6 (and_6_out, not_2_out, multiplexer_1_out[9]);
  and and_7 (and_7_out, not_2_out, multiplexer_1_out[8]);
  and and_8 (and_8_out, multiplexer_1_out[0], multiplexer_1_out[8]);
  and and_9 (and_9_out, multiplexer_1_out[0], multiplexer_1_out[10]);
  and and_10 (and_10_out, multiplexer_1_out[0], multiplexer_1_out[9]);
  Register register_2 (.D(controlled_buffer_7_out), .Q(register_2_q), .clk(and_1_out), .clr(or_1_out));  // open: en
  Counter #(.width(4), .max('hf)) counter_1 (
    .count(or_3_out), .Q(counter_1_q), .clk(and_1_out), .clr(or_1_out));  // open: load, D, carry
  and and_11 (and_11_out, multiplexer_1_out[1], not_2_out);
  and and_12 (and_12_out, multiplexer_1_out[1], multiplexer_1_out[0]);
  assign controlled_buffer_4_out = and_7_out ? Clock_q : 8'bz;  // Controlled_Buffer controlled_buffer_14
  assign controlled_buffer_15_out = multiplexer_1_out[4] ? controlled_buffer_4_out : 8'bz;  // Controlled_Buffer controlled_buffer_15
  not not_2 (not_2_out, multiplexer_1_out[0]);
  Multiplexer #(.width(12), .disabled(0), .enable("false")) multiplexer_1 (
    .in0(rom_1_data), .in1(multiplexer_2_out),
    .out({multiplexer_1_out[11:6], Write, multiplexer_1_out[4:0]}), .sel(and_4_out));
  ROM #(.dataWidth(12)) rom_1 (
    .addr({comparator_1_lt[7], register_2_q[2:0], counter_1_q}), .data(rom_1_data));  // open: sel
  Counter u_Clock (
    .load(multiplexer_1_out[4]), .D(controlled_buffer_15_out), .count(and_11_out), .Q(Clock_q),
    .clk(and_1_out), .clr(not_1_out));  // open: carry
  or or_2 (or_2_out, Address[3], Address[2], Address[1]);
  nor nor_1 (nor_1_out, multiplexer_1_out[11], multiplexer_1_out[10], multiplexer_1_out[9], multiplexer_1_out[8], multiplexer_1_out[7], multiplexer_1_out[6], Write, multiplexer_1_out[4], multiplexer_1_out[3], multiplexer_1_out[2], multiplexer_1_out[1], multiplexer_1_out[0]);
  and and_13 (and_13_out, or_3_out, and_4_out);
  Register register_3 (.D(Instruction_ID_in), .Q(Instruction_ID_out), .clk(and_1_out), .clr(Clear));  // open: en
  D_Flip_Flop d_ff_1 (.clk(and_1_out), .D(and_14_out), .Q(Clear), .reset(Clear));  // open: Qn, preset, en
  and and_14 (and_14_out, or_2_out, and_15_out);
  and and_15 (and_15_out, ~controlled_buffer_4_out[2], ~controlled_buffer_4_out[1], ~controlled_buffer_4_out[0], and_12_out, and_8_out);  // AND_Gate
  Counter #(.width(6), .max('h3f)) Macro_Counter (
    .count(and_13_out), .Q(Macro_Counter_q), .clk(and_1_out), .clr(not_3_out));  // open: load, D, carry
  not not_3 (not_3_out, and_4_out);
  assign Output = Output_Ready ? A_q : 8'bz;  // Controlled_Buffer controlled_buffer_16
  and and_16 (Output_Ready, multiplexer_1_out[0], ~multiplexer_1_out[1], ~multiplexer_1_out[2], ~multiplexer_1_out[3], ~multiplexer_1_out[4], ~Write, ~multiplexer_1_out[6], ~multiplexer_1_out[7], ~multiplexer_1_out[8], ~multiplexer_1_out[9], ~multiplexer_1_out[10], ~multiplexer_1_out[11]);  // AND_Gate
  D_Flip_Flop #(.trigger("falling")) d_ff_2 (
    .clk(Read), .D(Output_Ready), .Q(d_ff_2_q), .reset(not_4_out));  // open: Qn, preset, en
  not not_4 (not_4_out, Output_Ready);
  ROM #(.addrWidth(6), .dataWidth(12)) rom_2 (.addr(Macro_Counter_q), .data(rom_2_data));  // open: sel
  ROM #(.addrWidth(6), .dataWidth(12)) rom_3 (.addr(Macro_Counter_q), .data(rom_3_data));  // open: sel
  Pull_Resistor pull_resistor_4 (.node(Read));
  or or_3 (or_3_out, d_ff_2_q, not_4_out);
  Multiplexer #(.select(3), .width(12), .enable("false")) multiplexer_2 (
    .in0(rom_2_data), .in1(rom_3_data), .out(multiplexer_2_out), .sel(register_2_q[6:4]));  // open: in2, in3, in4, in5, in6, in7

  assign out_13 = Clock;

  // Notes on the sheet:
  //   Fixme:
  //   JLT
  //   Macro1: Dot3
  //   contents of rom_1 (hex, n*v repeats v):
  //   106 103 14*0 106 103 106 181 106 141 106 105 420 7*0 106 103 106 181 106 141 106 105 421 7*0 106 103
  //   106 181 106 141 106 105 820 7*0 106 103 106 181 106 141 106 105 821 7*0 106 103 106 111 12*0 106 103
  //   106 105 181 1 10*0 106 103 8 8 12*0 106 103 14*0 106 103 106 181 106 141 106 105 420 7*0 106 103 106
  //   181 106 141 106 105 421 7*0 106 103 106 181 106 141 106 105 820 7*0 106 103 106 181 106 141 106 105
  //   821 7*0 106 103 106 111 12*0 106 103 106 105 181 1 10*0 106 103 8 8
  //   MicroCode
  //   MO/DO AddO/SO AO/BO CO/MemO
  //   Ai Bi Memi Ci
  //   Lo, Li, inc/load, alt/output
  //   MacroCode
  //   0: Done
  //   1: Add
  //   2: Subtract
  //   3: Multiply
  //   4: Divide
  //   5: JLT
  //   6: Output
  //   7: Macro
  //   contents of rom_2 (hex, n*v repeats v):
  //   106 181 106 141 880 106 141 106 210 181 880 140 480 18 1
  //   contents of rom_3 (hex, n*v repeats v):
  //   106 181 106 141 880 106 141 106 210 181 880 140 480 18 106 106 141 106 210 181 880 140 480 18 1
  //   Macro's
  //   0: Dot2
endmodule

module GPU_Instruction_Fetcher (
  input  Ready__If_1__unit_will_not_fetch_instructions,
  input  Clock,
  input  [7:0] Core_Data__Data_output_or_input,
  input  [7:0] Data_In__Enter_Number_of_commands__then_commands_in_reverse_order,
  input  Clear__1_clears_buffers_contents,
  input  [3:0] Core_Address__Address_for_read_or_write,
  input  Dat_in_Use__If_1_unit_will_not_try_to_fetch_instructions,
  input  Write__If_1__will_write_data__else_will_read,
  input  [7:0] Instruction_ID_in,
  output Dat_in_Use__Will_output_1_if_it_or_later_unit_is_currently_fetching_instructions,
  output [7:0] Data_out,
  output Clock_2,
  output Execute,
  output Claimed__1_if_this_or_higher_unit_is_ready_to_fetch_Instructions,
  output [7:0] Instrution_ID_out
);

  wire and_1_out, and_2_out, and_3_out, and_4_out, and_5_out, and_6_out, and_7_out, and_8_out, nor_1_out,
       not_1_out, not_2_out, or_1_out, or_3_out, or_4_out, or_6_out, Running_qn;
  wire [3:0] counter_1_q, multiplexer_2_out;
  wire [7:0] controlled_buffer_1_out, multiplexer_1_out;

  and and_1 (and_1_out, or_1_out, ~or_3_out);  // AND_Gate
  and and_2 (and_2_out, or_3_out, ~Execute);  // AND_Gate
  and and_3 (and_3_out, counter_1_q[0], ~counter_1_q[1], ~counter_1_q[2], ~counter_1_q[3]);  // AND_Gate
  or or_1 (or_1_out, and_4_out, or_3_out);
  Register register_1 (
    .D(Instruction_ID_in), .en(and_1_out), .Q(Instrution_ID_out), .clk(Clock),
    .clr(Clear__1_clears_buffers_contents));
  or or_2 (Dat_in_Use__Will_output_1_if_it_or_later_unit_is_currently_fetching_instructions, Dat_in_Use__If_1_unit_will_not_try_to_fetch_instructions, and_2_out);
  or or_3 (or_3_out, counter_1_q[0], counter_1_q[1], counter_1_q[2], counter_1_q[3]);
  Counter #(.width(4), .max('hf), .ongoal("stay")) counter_1 (
    .load(or_1_out), .D(Data_In__Enter_Number_of_commands__then_commands_in_reverse_order[3:0]),
    .count(or_3_out), .Q(counter_1_q), .clk(Clock));  // open: carry, clr
  and and_4 (and_4_out, and_6_out, ~Execute, ~Ready__If_1__unit_will_not_fetch_instructions);  // AND_Gate
  D_Flip_Flop Running (
    .clk(Clock), .D(and_5_out), .Q(Execute), .Qn(Running_qn), .en(not_1_out),
    .reset(Clear__1_clears_buffers_contents));  // open: preset
  not not_1 (not_1_out, Execute);
  and and_5 (and_5_out, and_3_out, or_3_out);
  Pull_Resistor pull_resistor_1 (.node(Dat_in_Use__If_1_unit_will_not_try_to_fetch_instructions));
  Pull_Resistor pull_resistor_2 (.node(Ready__If_1__unit_will_not_fetch_instructions));
  and and_6 (and_6_out, ~or_3_out, ~Dat_in_Use__If_1_unit_will_not_try_to_fetch_instructions, ~Execute);  // AND_Gate
  or or_4 (or_4_out, Ready__If_1__unit_will_not_fetch_instructions, or_3_out, and_6_out);
  and and_7 (and_7_out, Running_qn, or_4_out);
  or or_5 (Claimed__1_if_this_or_higher_unit_is_ready_to_fetch_Instructions, and_7_out, Ready__If_1__unit_will_not_fetch_instructions);
  Multiplexer #(.width(8), .enable("false")) multiplexer_1 (
    .in0(Core_Data__Data_output_or_input),
    .in1(Data_In__Enter_Number_of_commands__then_commands_in_reverse_order), .out(multiplexer_1_out),
    .sel(or_3_out));
  Multiplexer #(.width(4), .enable("false")) multiplexer_2 (
    .in0(Core_Address__Address_for_read_or_write), .in1(counter_1_q), .out(multiplexer_2_out), .sel(or_3_out));
  nor nor_1 (nor_1_out, or_3_out, Execute);
  assign controlled_buffer_1_out = not_2_out ? multiplexer_1_out : 8'bz;  // Controlled_Buffer controlled_buffer_1
  RAM #(.addrWidth(4)) ram_1 (
    .addr(multiplexer_2_out), .data(controlled_buffer_1_out), .clk(Clock), .ld(or_6_out),
    .clr(Clear__1_clears_buffers_contents));  // open: sel
  or or_6 (or_6_out, nor_1_out, and_8_out);
  and and_8 (and_8_out, Execute, ~Write__If_1__will_write_data__else_will_read);  // AND_Gate
  Pull_Resistor pull_resistor_3 (.node(Write__If_1__will_write_data__else_will_read));
  not not_2 (not_2_out, or_6_out);
  assign Data_out = or_6_out ? controlled_buffer_1_out : 8'bz;  // Controlled_Buffer controlled_buffer_2
  Pull_Resistor pull_resistor_4 (.node(or_6_out));
  Pull_Resistor pull_resistor_5 (.node(Clear__1_clears_buffers_contents));

  assign Clock_2 = Clock;

  // Notes on the sheet:
  //   Data_out: pull=down
  //   Clear__1_clears_buffers_contents: pull=down
  //   Write__If_1__will_write_data__else_will_read: pull=down
  //   Syntax: How many instructions followed by instructions in reverse order
endmodule
