// Logisim project Utility.circ as structural Verilog: 3 circuits, main circuit Binary-Decimal-Converter
module Binary_Decimal_Converter (
  input  [7:0] Binary_In,
  output [7:0] out_2,
  output [7:0] out_3,
  output [7:0] out_4
);

  Pull_Resistor pull_resistor_1 (.node(Binary_In));
  ROM rom_1 (.addr(Binary_In), .data(out_2));  // open: sel
  ROM rom_2 (.addr(Binary_In), .data(out_3));  // open: sel
  ROM rom_3 (.addr(Binary_In), .data(out_4));  // open: sel

  // Notes on the sheet:
  //   contents of rom_1 (hex, n*v repeats v):
  //   100*e7 100*21 56*cb
  //   contents of rom_2 (hex, n*v repeats v):
  //   10*e7 10*21 10*cb 10*6b 10*2d 10*6e 10*ee 10*23 10*ef 10*6f 10*e7 10*21 10*cb 10*6b 10*2d 10*6e
  //   10*ee 10*23 10*ef 10*6f 10*e7 10*21 10*cb 10*6b 10*2d 6*6e
  //   contents of rom_3 (hex, n*v repeats v):
  //   e7 21 cb 6b 2d 6e ee 23 ef 2f e7 21 cb 6b 2d 6e ee 23 ef 2f e7 21 cb 6b 2d 6e ee 23 ef 2f e7 21 cb
  //   6b 2d 6e ee 23 ef 2f e7 21 cb 6b 2d 6e ee 23 ef 2f e7 21 cb 6b 2d 6e ee 23 ef 2f e7 21 cb 6b 2d 6e
  //   ee 23 ef 2f e7 21 cb 6b 2d 6e ee 23 ef 2f e7 21 cb 6b 2d 6e ee 23 ef 2f e7 21 cb 6b 2d 6e ee 23 ef
  //   2f e7 21 cb 6b 2d 6e ee 23 ef 2f e7 21 cb 6b 2d 6e ee 23 ef 2f e7 21 cb 6b 2d 6e ee 23 ef 2f e7 21
  //   cb 6b 2d 6e ee 23 ef 2f e7 21 cb 6b 2d 6e ee 23 ef 2f e7 21 cb 6b 2d 6e ee 23 ef 2f e7 21 cb 6b 2d
  //   6e ee 23 ef 2f e7 21 cb 6b 2d 6e ee 23 ef 2f e7 21 cb 6b 2d 6e ee 23 ef 2f e7 21 cb 6b 2d 6e ee 23
  //   ef 2f e7 21 cb 6b 2d 6e ee 23 ef 2f e7 21 cb 6b 2d 6e ee 23 ef 2f e7 21 cb 6b 2d 6e ee 23 ef 2f e7
  //   21 cb 6b 2d 6e ee 23 ef 2f e7 21 cb 6b 2d 6e ee 23 ef 2f e7 21 cb 6b 2d 6e
endmodule

module Millienium_Timer (
);

  wire _1_Hour_q, _1_Minute_q, _1_ms_q, _1_second_q, _1_years_q, _3_days_q, _17_years_q, clock_1_out,
       t_ff_1_q, t_ff_2_q, t_ff_3_q, t_ff_4_q, t_ff_5_q, t_ff_6_q, t_ff_7_q, t_ff_8_q, t_ff_9_q, t_ff_10_q,
       t_ff_11_q, t_ff_12_q, t_ff_13_q, t_ff_14_q, t_ff_15_q, t_ff_16_q, t_ff_17_q, t_ff_18_q, t_ff_19_q,
       t_ff_20_q, t_ff_21_q, t_ff_22_q, t_ff_23_q, t_ff_24_q, t_ff_25_q, t_ff_26_q, t_ff_27_q, t_ff_28_q,
       t_ff_29_q, t_ff_30_q, t_ff_31_q, t_ff_32_q, t_ff_33_q, t_ff_34_q, t_ff_35_q, t_ff_36_q, t_ff_37_q,
       t_ff_38_q;

  Clock clock_1 (.out(clock_1_out));
  T_Flip_Flop #(.trigger("falling")) _1_ms (.clk(clock_1_out), .T(1'b1), .Q(_1_ms_q));  // open: Qn, preset, reset, en
  T_Flip_Flop #(.trigger("falling")) t_ff_1 (.clk(t_ff_38_q), .T(1'b1), .Q(t_ff_1_q));  // open: Qn, preset, reset, en
  T_Flip_Flop #(.trigger("falling")) t_ff_2 (.clk(t_ff_3_q), .T(1'b1), .Q(t_ff_2_q));  // open: Qn, preset, reset, en
  T_Flip_Flop #(.trigger("falling")) t_ff_3 (.clk(_1_ms_q), .T(1'b1), .Q(t_ff_3_q));  // open: Qn, preset, reset, en
  T_Flip_Flop #(.trigger("falling")) t_ff_4 (.clk(t_ff_1_q), .T(1'b1), .Q(t_ff_4_q));  // open: Qn, preset, reset, en
  T_Flip_Flop #(.trigger("falling")) t_ff_5 (.clk(t_ff_4_q), .T(1'b1), .Q(t_ff_5_q));  // open: Qn, preset, reset, en
  T_Flip_Flop #(.trigger("falling")) t_ff_6 (.clk(t_ff_2_q), .T(1'b1), .Q(t_ff_6_q));  // open: Qn, preset, reset, en
  T_Flip_Flop #(.trigger("falling")) t_ff_7 (.clk(t_ff_5_q), .T(1'b1), .Q(t_ff_7_q));  // open: Qn, preset, reset, en
  T_Flip_Flop #(.trigger("falling")) t_ff_8 (.clk(t_ff_6_q), .T(1'b1), .Q(t_ff_8_q));  // open: Qn, preset, reset, en
  T_Flip_Flop #(.trigger("falling")) t_ff_9 (.clk(t_ff_8_q), .T(1'b1), .Q(t_ff_9_q));  // open: Qn, preset, reset, en
  T_Flip_Flop #(.trigger("falling")) t_ff_10 (.clk(_3_days_q), .T(1'b1), .Q(t_ff_10_q));  // open: Qn, preset, reset, en
  T_Flip_Flop #(.trigger("falling")) _3_days (.clk(t_ff_7_q), .T(1'b1), .Q(_3_days_q));  // open: Qn, preset, reset, en
  T_Flip_Flop #(.trigger("falling")) t_ff_11 (.clk(t_ff_9_q), .T(1'b1), .Q(t_ff_11_q));  // open: Qn, preset, reset, en
  T_Flip_Flop #(.trigger("falling")) t_ff_12 (.clk(t_ff_11_q), .T(1'b1), .Q(t_ff_12_q));  // open: Qn, preset, reset, en
  T_Flip_Flop #(.trigger("falling")) t_ff_13 (.clk(t_ff_10_q), .T(1'b1), .Q(t_ff_13_q));  // open: Qn, preset, reset, en
  T_Flip_Flop #(.trigger("falling")) t_ff_14 (.clk(t_ff_13_q), .T(1'b1), .Q(t_ff_14_q));  // open: Qn, preset, reset, en
  T_Flip_Flop #(.trigger("falling")) t_ff_15 (.clk(t_ff_12_q), .T(1'b1), .Q(t_ff_15_q));  // open: Qn, preset, reset, en
  T_Flip_Flop #(.trigger("falling")) t_ff_16 (.clk(t_ff_14_q), .T(1'b1), .Q(t_ff_16_q));  // open: Qn, preset, reset, en
  T_Flip_Flop #(.trigger("falling")) _1_second (
    .clk(t_ff_17_q), .T(1'b1), .Q(_1_second_q));  // open: Qn, preset, reset, en
  T_Flip_Flop #(.trigger("falling")) t_ff_17 (.clk(t_ff_15_q), .T(1'b1), .Q(t_ff_17_q));  // open: Qn, preset, reset, en
  T_Flip_Flop #(.trigger("falling")) t_ff_18 (.clk(t_ff_19_q), .T(1'b1), .Q(t_ff_18_q));  // open: Qn, preset, reset, en
  T_Flip_Flop #(.trigger("falling")) t_ff_19 (.clk(t_ff_16_q), .T(1'b1), .Q(t_ff_19_q));  // open: Qn, preset, reset, en
  T_Flip_Flop #(.trigger("falling")) t_ff_20 (
    .clk(_1_second_q), .T(1'b1), .Q(t_ff_20_q));  // open: Qn, preset, reset, en
  T_Flip_Flop #(.trigger("falling")) _1_years (
    .clk(t_ff_18_q), .T(1'b1), .Q(_1_years_q));  // open: Qn, preset, reset, en
  T_Flip_Flop #(.trigger("falling")) t_ff_21 (.clk(t_ff_22_q), .T(1'b1), .Q(t_ff_21_q));  // open: Qn, preset, reset, en
  T_Flip_Flop #(.trigger("falling")) t_ff_22 (.clk(t_ff_20_q), .T(1'b1), .Q(t_ff_22_q));  // open: Qn, preset, reset, en
  T_Flip_Flop #(.trigger("falling")) t_ff_23 (
    .clk(_1_years_q), .T(1'b1), .Q(t_ff_23_q));  // open: Qn, preset, reset, en
  T_Flip_Flop #(.trigger("falling")) t_ff_24 (.clk(t_ff_23_q), .T(1'b1), .Q(t_ff_24_q));  // open: Qn, preset, reset, en
  T_Flip_Flop #(.trigger("falling")) t_ff_25 (.clk(t_ff_26_q), .T(1'b1), .Q(t_ff_25_q));  // open: Qn, preset, reset, en
  T_Flip_Flop #(.trigger("falling")) t_ff_26 (.clk(t_ff_21_q), .T(1'b1), .Q(t_ff_26_q));  // open: Qn, preset, reset, en
  T_Flip_Flop #(.trigger("falling")) t_ff_27 (.clk(t_ff_24_q), .T(1'b1), .Q(t_ff_27_q));  // open: Qn, preset, reset, en
  T_Flip_Flop #(.trigger("falling")) _17_years (
    .clk(t_ff_27_q), .T(1'b1), .Q(_17_years_q));  // open: Qn, preset, reset, en
  T_Flip_Flop #(.trigger("falling")) _1_Minute (
    .clk(t_ff_25_q), .T(1'b1), .Q(_1_Minute_q));  // open: Qn, preset, reset, en
  T_Flip_Flop #(.trigger("falling")) t_ff_28 (
    .clk(_17_years_q), .T(1'b1), .Q(t_ff_28_q));  // open: Qn, preset, reset, en
  T_Flip_Flop #(.trigger("falling")) t_ff_29 (
    .clk(_1_Minute_q), .T(1'b1), .Q(t_ff_29_q));  // open: Qn, preset, reset, en
  T_Flip_Flop #(.trigger("falling")) t_ff_30 (.clk(t_ff_29_q), .T(1'b1), .Q(t_ff_30_q));  // open: Qn, preset, reset, en
  T_Flip_Flop #(.trigger("falling")) t_ff_31 (.clk(t_ff_28_q), .T(1'b1), .Q(t_ff_31_q));  // open: Qn, preset, reset, en
  T_Flip_Flop #(.trigger("falling")) t_ff_32 (.clk(t_ff_31_q), .T(1'b1), .Q(t_ff_32_q));  // open: Qn, preset, reset, en
  T_Flip_Flop #(.trigger("falling")) t_ff_33 (.clk(t_ff_30_q), .T(1'b1), .Q(t_ff_33_q));  // open: Qn, preset, reset, en
  T_Flip_Flop #(.trigger("falling")) t_ff_34 (.clk(t_ff_32_q), .T(1'b1), .Q(t_ff_34_q));  // open: Qn, preset, reset, en
  T_Flip_Flop #(.trigger("falling")) t_ff_35 (.clk(t_ff_36_q), .T(1'b1), .Q(t_ff_35_q));  // open: Qn, preset, reset, en
  T_Flip_Flop #(.trigger("falling")) t_ff_36 (.clk(t_ff_33_q), .T(1'b1), .Q(t_ff_36_q));  // open: Qn, preset, reset, en
  T_Flip_Flop #(.trigger("falling")) t_ff_37 (.clk(t_ff_34_q), .T(1'b1), .Q(t_ff_37_q));  // open: Qn, preset, reset, en
  T_Flip_Flop #(.trigger("falling")) _1089_years (.clk(t_ff_37_q), .T(1'b1));  // open: Q, Qn, preset, reset, en
  T_Flip_Flop #(.trigger("falling")) _1_Hour (.clk(t_ff_35_q), .T(1'b1), .Q(_1_Hour_q));  // open: Qn, preset, reset, en
  T_Flip_Flop #(.trigger("falling")) t_ff_38 (.clk(_1_Hour_q), .T(1'b1), .Q(t_ff_38_q));  // open: Qn, preset, reset, en

  // Notes on the sheet:
  //   46 flip flops
endmodule

module Pulse_Generator (
  input  Input,
  input  Rising_Falling__If_1__will_pulse_on_falling_edge,
  output Output
);

  wire and_1_out, nor_1_out, not_1_out, not_2_out;

  Pull_Resistor pull_resistor_1 (.node(Input));
  and and_1 (and_1_out, Input, not_1_out);
  not not_1 (not_1_out, Input);
  nor nor_1 (nor_1_out, Input, not_2_out);
  not not_2 (not_2_out, Input);
  Multiplexer #(.enable("false")) multiplexer_1 (
    .in0(and_1_out), .in1(nor_1_out), .out(Output), .sel(Rising_Falling__If_1__will_pulse_on_falling_edge));
  Pull_Resistor pull_resistor_2 (.node(Rising_Falling__If_1__will_pulse_on_falling_edge));
endmodule
